// Logisim project 数码管输出设计.circ as structural Verilog: 10 circuits, main circuit main
module main (
  input  D0,
  input  in_2,
  input  D1,
  input  D2,
  input  D3
);

  wire digital_1_a, digital_1_b, digital_1_c, digital_1_d, digital_1_e, digital_1_f, digital_1_g,
       \三态门_1_out_6 , \三态门_1_out_7 , \三态门_1_out_8 , \三态门_1_out_9 ;

  \三态门  \u_三态门_1  (
    .in_2(D0), .in_3(D1), .in_4(D2), .in_5(D3), .in_1(in_2), .out_6(\三态门_1_out_6 ), .out_7(\三态门_1_out_7 ),
    .out_8(\三态门_1_out_8 ), .out_9(\三态门_1_out_9 ));
  Digital digital_1 (
    .D0(\三态门_1_out_6 ), .D1(\三态门_1_out_7 ), .D2(\三态门_1_out_8 ), .D3(\三态门_1_out_9 ), .a(digital_1_a),
    .b(digital_1_b), .c(digital_1_c), .d(digital_1_d), .e(digital_1_e), .f(digital_1_f), .g(digital_1_g));
  _7_Segment_Display #(.active("false")) u_7_segment_display_1 (
    .g(digital_1_g), .f(digital_1_f), .a(digital_1_a), .b(digital_1_b), .e(digital_1_e), .d(digital_1_d),
    .c(digital_1_c), .dp(1'b1));
endmodule

module Digital_a (
  input  D3,
  input  D2,
  input  D1,
  input  D0,
  output a
);

  wire and_1_out, and_2_out, and_3_out, and_4_out, D0_out, D1_out, D2_out, D3_out;

  not u_D3 (D3_out, D3);
  not u_D1 (D1_out, D1);
  not u_D0 (D0_out, D0);
  not u_D2 (D2_out, D2);
  and and_1 (and_1_out, D3_out, D2_out, D1_out, D0);
  and and_2 (and_2_out, D3_out, D2, D1_out, D0_out);
  and and_3 (and_3_out, D3, D2_out, D1, D0);
  and and_4 (and_4_out, D3, D2, D1_out, D0);
  or or_1 (a, and_1_out, and_2_out, and_3_out, and_4_out);
endmodule

module Digital_b (
  input  D3,
  input  D2,
  input  D1,
  input  D0,
  output b
);

  wire and_1_out, and_2_out, and_3_out, and_4_out, D0_out, D1_out, D3_out;

  not u_D3 (D3_out, D3);
  not u_D1 (D1_out, D1);
  not u_D0 (D0_out, D0);
  and and_1 (and_1_out, D2, D1, D0_out);
  and and_2 (and_2_out, D3, D1, D0);
  and and_3 (and_3_out, D3, D2, D0_out);
  and and_4 (and_4_out, D3_out, D2, D1_out, D0);
  or or_1 (b, and_1_out, and_2_out, and_3_out, and_4_out);
endmodule

module Digital_c (
  input  D3,
  input  D2,
  input  D1,
  input  D0,
  output c
);

  wire and_1_out, and_2_out, and_3_out, not_1_out, not_2_out, not_3_out;

  not not_1 (not_1_out, D3);
  not not_2 (not_2_out, D2);
  not not_3 (not_3_out, D0);
  and and_1 (and_1_out, not_1_out, not_2_out, D1, not_3_out);
  and and_2 (and_2_out, D3, D2, D1);
  and and_3 (and_3_out, D3, D2, not_3_out);
  or or_1 (c, and_1_out, and_2_out, and_3_out);
endmodule

module Digital_d (
  input  D3,
  input  D2,
  input  D1,
  input  D0,
  output d
);

  wire and_1_out, and_2_out, and_3_out, and_4_out, not_1_out, not_2_out, not_3_out, not_4_out;

  not not_1 (not_1_out, D3);
  not not_2 (not_2_out, D2);
  not not_3 (not_3_out, D1);
  not not_4 (not_4_out, D0);
  and and_1 (and_1_out, not_1_out, not_2_out, not_3_out, D0);
  and and_2 (and_2_out, not_1_out, D2, not_3_out, not_4_out);
  and and_3 (and_3_out, D2, D1, D0);
  and and_4 (and_4_out, D3, not_2_out, D1, not_4_out);
  or or_1 (d, and_1_out, and_2_out, and_3_out, and_4_out);
endmodule

module Digital_e (
  input  D3,
  input  D2,
  input  D1,
  input  D0,
  output e
);

  wire and_1_out, and_2_out, and_3_out, not_1_out, not_2_out, not_3_out;

  not not_1 (not_1_out, D3);
  not not_2 (not_2_out, D2);
  not not_3 (not_3_out, D1);
  and and_1 (and_1_out, not_1_out, D0);
  and and_2 (and_2_out, not_1_out, D2, not_3_out);
  and and_3 (and_3_out, not_2_out, not_3_out, D0);
  or or_1 (e, and_1_out, and_2_out, and_3_out);
endmodule

module Digital_f (
  input  D3,
  input  D2,
  input  D1,
  input  D0,
  output f
);

  wire and_1_out, and_2_out, and_3_out, and_4_out, not_1_out, not_2_out, not_3_out;

  not not_1 (not_1_out, D3);
  not not_2 (not_2_out, D2);
  not not_3 (not_3_out, D1);
  and and_1 (and_1_out, not_1_out, not_2_out, D1);
  and and_2 (and_2_out, not_1_out, not_2_out, D0);
  and and_3 (and_3_out, not_1_out, D1, D0);
  and and_4 (and_4_out, D3, D2, not_3_out, D0);
  or or_1 (f, and_1_out, and_2_out, and_3_out, and_4_out);
endmodule

module Digital_g (
  input  D3,
  input  D2,
  input  D1,
  input  D0,
  output g
);

  wire and_1_out, and_2_out, and_3_out, not_1_out, not_2_out, not_3_out, not_4_out;

  not not_1 (not_1_out, D3);
  not not_2 (not_2_out, D2);
  not not_3 (not_3_out, D1);
  not not_4 (not_4_out, D0);
  and and_1 (and_1_out, not_1_out, not_2_out, not_3_out);
  and and_2 (and_2_out, not_1_out, D2, D1, D0);
  and and_3 (and_3_out, D3, D2, not_3_out, not_4_out);
  or or_1 (g, and_1_out, and_2_out, and_3_out);
endmodule

// 7seg
module Digital (
  input  D0,
  input  D1,
  input  D2,
  input  D3,
  output a,
  output b,
  output c,
  output d,
  output e,
  output f,
  output g
);

  Digital_a digital_a_1 (.D3(D3), .D2(D2), .D1(D1), .D0(D0), .a(a));
  Digital_b digital_b_1 (.D3(D3), .D2(D2), .D1(D1), .D0(D0), .b(b));
  Digital_c digital_c_1 (.D3(D3), .D2(D2), .D1(D1), .D0(D0), .c(c));
  Digital_d digital_d_1 (.D3(D3), .D2(D2), .D1(D1), .D0(D0), .d(d));
  Digital_e digital_e_1 (.D3(D3), .D2(D2), .D1(D1), .D0(D0), .e(e));
  Digital_f digital_f_1 (.D3(D3), .D2(D2), .D1(D1), .D0(D0), .f(f));
  Digital_g digital_g_1 (.D3(D3), .D2(D2), .D1(D1), .D0(D0), .g(g));
endmodule

module \三态门  (
  input  in_1,
  input  in_2,
  input  in_3,
  input  in_4,
  input  in_5,
  output out_6,
  output out_7,
  output out_8,
  output out_9
);

  and and_1 (out_6, in_2, in_1);
  and and_2 (out_7, in_3, in_1);
  and and_3 (out_8, in_4, in_1);
  and and_4 (out_9, in_5, in_1);
endmodule
