// Logisim project 多端口输入.circ as structural Verilog: 6 circuits, main circuit main
module main (
  input  i0,
  input  in_2,
  input  in_3,
  input  i1,
  input  i2,
  input  i3,
  input  i4,
  input  i5,
  input  in_9,
  input  i6,
  input  i7,
  input  i8,
  input  i9,
  input  i10,
  input  i11,
  input  i12,
  input  i13,
  input  i14,
  input  i15,
  input  i0_2,
  input  i1_2,
  input  in_22,
  input  in_23,
  input  i2_2,
  input  i3_2,
  input  i4_2,
  input  i5_2,
  input  i6_2,
  input  i7_2,
  input  i8_2,
  input  i9_2,
  input  i10_2,
  input  i11_2,
  input  i12_2,
  input  i13_2,
  input  i14_2,
  input  i15_2
);

  wire double16_1_y0, double16_1_y1, double16_1_y2, double16_1_y3, double16_1_y4, double16_1_y5,
       double16_1_y6, double16_1_y7, n2seg_1_out_10, n2seg_1_out_11, n2seg_1_out_12, n2seg_1_out_13,
       n2seg_1_out_14, n2seg_1_out_15, n2seg_1_out_16, n2seg_1_out_17, n2seg_1_out_18, n2seg_1_out_19,
       n2seg_1_out_20, n2seg_1_out_21, n2seg_1_out_22, n2seg_1_out_23;

  double16 double16_1 (
    .i0(i0), .i1(i1), .i2(i2), .i3(i3), .i4(i4), .i5(i5), .i6(i6), .i7(i7), .i8(i8), .i9(i9), .i10(i10),
    .i11(i11), .i12(i12), .i13(i13), .i14(i14), .i15(i15), .i0_2(i0_2), .i1_2(i1_2), .i2_2(i2_2),
    .i3_2(i3_2), .i4_2(i4_2), .i5_2(i5_2), .i6_2(i6_2), .i7_2(i7_2), .i8_2(i8_2), .i9_2(i9_2), .i10_2(i10_2),
    .i11_2(i11_2), .i12_2(i12_2), .i13_2(i13_2), .i14_2(i14_2), .i15_2(i15_2), .Y0(double16_1_y0),
    .Y1(double16_1_y1), .Y2(double16_1_y2), .Y3(double16_1_y3), .Y4(double16_1_y4), .Y5(double16_1_y5),
    .Y6(double16_1_y6), .Y7(double16_1_y7), .in_4(in_2), .in_15(in_3), .in_22(in_22), .in_23(in_23));
  LED #(.active("true")) led_1 (.in(double16_1_y1));
  LED #(.active("true")) led_2 (.in(double16_1_y2));
  LED #(.active("true")) led_3 (.in(double16_1_y0));
  LED #(.active("true")) led_4 (.in(double16_1_y3));
  LED #(.active("true")) led_5 (.in(double16_1_y6));
  LED #(.active("true")) led_6 (.in(double16_1_y5));
  LED #(.active("true")) led_7 (.in(double16_1_y7));
  LED #(.active("true")) led_8 (.in(double16_1_y4));
  _2seg u_2seg_1 (
    .i0(double16_1_y4), .i1(double16_1_y5), .i2(double16_1_y6), .i3(double16_1_y7), .i4(double16_1_y0),
    .i5(double16_1_y1), .i6(double16_1_y2), .i7(double16_1_y3), .out_10(n2seg_1_out_10),
    .out_11(n2seg_1_out_11), .out_12(n2seg_1_out_12), .out_13(n2seg_1_out_13), .out_14(n2seg_1_out_14),
    .out_15(n2seg_1_out_15), .out_16(n2seg_1_out_16), .out_17(n2seg_1_out_17), .out_18(n2seg_1_out_18),
    .out_19(n2seg_1_out_19), .out_20(n2seg_1_out_20), .out_21(n2seg_1_out_21), .out_22(n2seg_1_out_22),
    .out_23(n2seg_1_out_23), .in_2(in_9));
  _7_Segment_Display #(.active("false")) u_7_segment_display_1 (
    .g(n2seg_1_out_23), .f(n2seg_1_out_22), .a(n2seg_1_out_17), .b(n2seg_1_out_18), .e(n2seg_1_out_21),
    .d(n2seg_1_out_20), .c(n2seg_1_out_19), .dp(1'b1));
  _7_Segment_Display #(.active("false")) u_7_segment_display_2 (
    .g(n2seg_1_out_16), .f(n2seg_1_out_15), .a(n2seg_1_out_10), .b(n2seg_1_out_11), .e(n2seg_1_out_14),
    .d(n2seg_1_out_13), .c(n2seg_1_out_12), .dp(1'b1));
endmodule

module _16_4 (
  input  i0,
  input  i1,
  input  i2,
  input  i3,
  input  i4,
  input  i5,
  input  i6,
  input  i7,
  input  i0_2,
  input  i1_2,
  input  i2_2,
  input  i3_2,
  input  i4_2,
  input  i5_2,
  input  i6_2,
  input  i7_2,
  output y0,
  output y1,
  output y2,
  output y3
);

  or or_1 (y0, i1, i3, i5, i7, i1_2, i3_2, i5_2, i7_2);
  or or_2 (y1, i2, i3, i6, i7, i2_2, i3_2, i6_2, i7_2);
  or or_3 (y2, i4, i5, i6, i7, i4_2, i5_2, i6_2, i7_2);
  or or_4 (y3, i0_2, i1_2, i2_2, i3_2, i4_2, i5_2, i6_2, i7_2);
endmodule

module key16 (
  input  i0,
  input  i1,
  input  i2,
  input  i3,
  input  i4,
  input  i5,
  input  i6,
  input  i7,
  input  i0_2,
  input  i1_2,
  input  i2_2,
  input  in_12,
  input  i3_2,
  input  i4_2,
  input  i5_2,
  input  i6_2,
  input  i7_2,
  input  i0_3,
  input  i1_3,
  input  i2_3,
  input  i3_3,
  input  i4_3,
  input  i5_3,
  input  i6_3,
  input  i7_3,
  input  i0_4,
  input  i1_4,
  input  i2_4,
  input  i3_4,
  input  i4_4,
  input  i5_4,
  input  i6_4,
  input  i7_4,
  output out_34,
  output out_35,
  output out_36,
  output out_37,
  output out_38,
  output out_39,
  output out_40,
  output out_41
);

  wire n16_4_1_y0, n16_4_1_y1, n16_4_1_y2, n16_4_1_y3, n16_4_2_y0, n16_4_2_y1, n16_4_2_y2, n16_4_2_y3;

  _16_4 u_16_4_1 (
    .i0(i0), .i1(i1), .i2(i2), .i3(i3), .i4(i4), .i5(i5), .i6(i6), .i7(i7), .i0_2(i0_2), .i1_2(i1_2),
    .i2_2(i2_2), .i3_2(i3_2), .i4_2(i4_2), .i5_2(i5_2), .i6_2(i6_2), .i7_2(i7_2), .y0(n16_4_1_y0),
    .y1(n16_4_1_y1), .y2(n16_4_1_y2), .y3(n16_4_1_y3));
  _16_4 u_16_4_2 (
    .i0(i0_3), .i1(i1_3), .i2(i2_3), .i3(i3_3), .i4(i4_3), .i5(i5_3), .i6(i6_3), .i7(i7_3), .i0_2(i0_4),
    .i1_2(i1_4), .i2_2(i2_4), .i3_2(i3_4), .i4_2(i4_4), .i5_2(i5_4), .i6_2(i6_4), .i7_2(i7_4),
    .y0(n16_4_2_y0), .y1(n16_4_2_y1), .y2(n16_4_2_y2), .y3(n16_4_2_y3));
  C8 c8_1 (
    .in_2(n16_4_1_y0), .in_3(n16_4_1_y1), .in_4(n16_4_1_y2), .in_5(n16_4_1_y3), .in_6(n16_4_2_y0),
    .in_7(n16_4_2_y1), .in_8(n16_4_2_y2), .in_9(n16_4_2_y3), .out_10(out_34), .out_11(out_35),
    .out_12(out_36), .out_13(out_37), .out_14(out_38), .out_15(out_39), .out_16(out_40), .out_17(out_41),
    .in_1(in_12));
endmodule

module C8 (
  input  in_1,
  input  in_2,
  input  in_3,
  input  in_4,
  input  in_5,
  input  in_6,
  input  in_7,
  input  in_8,
  input  in_9,
  output out_10,
  output out_11,
  output out_12,
  output out_13,
  output out_14,
  output out_15,
  output out_16,
  output out_17
);

  assign out_10 = in_1 ? in_2 : 1'bz;  // Controlled_Buffer controlled_buffer_1
  assign out_11 = in_1 ? in_3 : 1'bz;  // Controlled_Buffer controlled_buffer_2
  assign out_12 = in_1 ? in_4 : 1'bz;  // Controlled_Buffer controlled_buffer_3
  assign out_13 = in_1 ? in_5 : 1'bz;  // Controlled_Buffer controlled_buffer_4
  assign out_14 = in_1 ? in_6 : 1'bz;  // Controlled_Buffer controlled_buffer_5
  assign out_15 = in_1 ? in_7 : 1'bz;  // Controlled_Buffer controlled_buffer_6
  assign out_16 = in_1 ? in_8 : 1'bz;  // Controlled_Buffer controlled_buffer_7
  assign out_17 = in_1 ? in_9 : 1'bz;  // Controlled_Buffer controlled_buffer_8
endmodule

module double16 (
  input  i0,
  input  i1,
  input  i2,
  input  in_4,
  input  i3,
  input  i4,
  input  i5,
  input  i6,
  input  i7,
  input  i8,
  input  i9,
  input  i10,
  input  i11,
  input  i12,
  input  in_15,
  input  i13,
  input  i14,
  input  i15,
  input  i0_2,
  input  i1_2,
  input  i2_2,
  input  in_22,
  input  in_23,
  input  i3_2,
  input  i4_2,
  input  i5_2,
  input  i6_2,
  input  i7_2,
  input  i8_2,
  input  i9_2,
  input  i10_2,
  input  i11_2,
  input  i12_2,
  input  i13_2,
  input  i14_2,
  input  i15_2,
  output Y0,
  output Y1,
  output Y2,
  output Y3,
  output Y4,
  output Y5,
  output Y6,
  output Y7
);

  wire and_1_out, n16_4_1_y0, n16_4_1_y1, n16_4_1_y2, n16_4_1_y3, n16_4_2_y0, n16_4_2_y1, n16_4_2_y2,
       n16_4_2_y3, reg8_1_out_10, reg8_1_out_11, reg8_1_out_12, reg8_1_out_13, reg8_1_out_14, reg8_1_out_15,
       reg8_1_out_16, reg8_1_out_17;

  _16_4 u_16_4_1 (
    .i0(i0), .i1(i1), .i2(i2), .i3(i3), .i4(i4), .i5(i5), .i6(i6), .i7(i7), .i0_2(i8), .i1_2(i9), .i2_2(i10),
    .i3_2(i11), .i4_2(i12), .i5_2(i13), .i6_2(i14), .i7_2(i15), .y0(n16_4_1_y0), .y1(n16_4_1_y1),
    .y2(n16_4_1_y2), .y3(n16_4_1_y3));
  _16_4 u_16_4_2 (
    .i0(i0_2), .i1(i1_2), .i2(i2_2), .i3(i3_2), .i4(i4_2), .i5(i5_2), .i6(i6_2), .i7(i7_2), .i0_2(i8_2),
    .i1_2(i9_2), .i2_2(i10_2), .i3_2(i11_2), .i4_2(i12_2), .i5_2(i13_2), .i6_2(i14_2), .i7_2(i15_2),
    .y0(n16_4_2_y0), .y1(n16_4_2_y1), .y2(n16_4_2_y2), .y3(n16_4_2_y3));
  reg8 reg8_1 (
    .out_10(reg8_1_out_10), .out_11(reg8_1_out_11), .out_12(reg8_1_out_12), .out_13(reg8_1_out_13),
    .out_14(reg8_1_out_14), .out_15(reg8_1_out_15), .out_16(reg8_1_out_16), .out_17(reg8_1_out_17),
    .in_2(n16_4_1_y0), .in_3(n16_4_1_y1), .in_4(n16_4_1_y2), .in_5(n16_4_1_y3), .in_6(n16_4_2_y0),
    .in_7(n16_4_2_y1), .in_8(n16_4_2_y2), .in_9(n16_4_2_y3), .in_1(in_22));
  C8 c8_1 (
    .in_2(n16_4_1_y0), .in_3(n16_4_1_y1), .in_4(n16_4_1_y2), .in_5(n16_4_1_y3), .in_6(n16_4_2_y0),
    .in_7(n16_4_2_y1), .in_8(n16_4_2_y2), .in_9(n16_4_2_y3), .out_10(Y0), .out_11(Y1), .out_12(Y2),
    .out_13(Y3), .out_14(Y4), .out_15(Y5), .out_16(Y6), .out_17(Y7), .in_1(in_4));
  and and_1 (and_1_out, reg8_1_out_13, in_23);
  C8 c8_2 (
    .in_2(reg8_1_out_10), .in_3(reg8_1_out_11), .in_4(reg8_1_out_12), .in_5(and_1_out), .in_6(reg8_1_out_14),
    .in_7(reg8_1_out_15), .in_8(reg8_1_out_16), .in_9(reg8_1_out_17), .out_10(Y0), .out_11(Y1), .out_12(Y2),
    .out_13(Y3), .out_14(Y4), .out_15(Y5), .out_16(Y6), .out_17(Y7), .in_1(in_15));
endmodule

module _2seg (
  input  i0,
  input  in_2,
  input  i1,
  input  i2,
  input  i3,
  input  i4,
  input  i5,
  input  i6,
  input  i7,
  output out_10,
  output out_11,
  output out_12,
  output out_13,
  output out_14,
  output out_15,
  output out_16,
  output out_17,
  output out_18,
  output out_19,
  output out_20,
  output out_21,
  output out_22,
  output out_23
);

  wire c8_1_out_10, c8_1_out_11, c8_1_out_12, c8_1_out_13, c8_1_out_14, c8_1_out_15, c8_1_out_16, c8_1_out_17;

  C8 c8_1 (
    .in_2(i0), .in_3(i1), .in_4(i2), .in_5(i3), .in_6(i4), .in_7(i5), .in_8(i6), .in_9(i7),
    .out_10(c8_1_out_10), .out_11(c8_1_out_11), .out_12(c8_1_out_12), .out_13(c8_1_out_13),
    .out_14(c8_1_out_14), .out_15(c8_1_out_15), .out_16(c8_1_out_16), .out_17(c8_1_out_17), .in_1(in_2));
  Digital digital_1 (
    .D0(c8_1_out_10), .D1(c8_1_out_11), .D2(c8_1_out_12), .D3(c8_1_out_13), .a(out_10), .b(out_11),
    .c(out_12), .d(out_13), .e(out_14), .f(out_15), .g(out_16));
  Digital digital_2 (
    .D0(c8_1_out_14), .D1(c8_1_out_15), .D2(c8_1_out_16), .D3(c8_1_out_17), .a(out_17), .b(out_18),
    .c(out_19), .d(out_20), .e(out_21), .f(out_22), .g(out_23));
endmodule
