// Logisim project 运算器设计.circ as structural Verilog: 7 circuits, main circuit main
module main (
  input  i0,
  input  i1,
  input  i2,
  input  i3,
  input  i4,
  input  i5,
  input  i6,
  input  i7,
  input  i8,
  input  i9,
  input  i10,
  input  i11,
  input  i12,
  input  i13,
  input  i14,
  input  i15,
  input  i0_2,
  input  i1_2,
  input  i2_2,
  input  i3_2,
  input  i4_2,
  input  i5_2,
  input  i6_2,
  input  i7_2,
  input  i8_2,
  input  i9_2,
  input  i10_2,
  input  i11_2,
  input  i12_2,
  input  i13_2,
  input  i14_2,
  input  i15_2,
  input  I0_3,
  input  I1_3,
  input  WI1,
  input  I1en,
  input  O0,
  input  RA,
  input  Rt,
  input  RB,
  input  Ain,
  input  Aout,
  input  aout_2,
  output out_44
);

  wire A_out_10, A_out_11, A_out_12, A_out_13, A_out_14, A_out_15, A_out_16, A_out_17, Ain_out_10,
       Ain_out_11, Ain_out_12, Ain_out_13, Ain_out_14, Ain_out_15, Ain_out_16, Ain_out_17, B_out_10,
       B_out_11, B_out_12, B_out_13, B_out_14, B_out_15, B_out_16, B_out_17, C_out_10, C_out_11, C_out_12,
       C_out_13, C_out_14, C_out_15, C_out_16, C_out_17, double16_1_y0, double16_1_y1, double16_1_y2,
       double16_1_y3, double16_1_y4, double16_1_y5, double16_1_y6, double16_1_y7, n2seg_1_out_10,
       n2seg_1_out_11, n2seg_1_out_12, n2seg_1_out_13, n2seg_1_out_14, n2seg_1_out_15, n2seg_1_out_16,
       n2seg_1_out_17, n2seg_1_out_18, n2seg_1_out_19, n2seg_1_out_20, n2seg_1_out_21, n2seg_1_out_22,
       n2seg_1_out_23, n8add_1_s0, n8add_1_s1, n8add_1_s2, n8add_1_s3, n8add_1_s4, n8add_1_s5, n8add_1_s6,
       n8add_1_s7;

  double16 double16_1 (
    .i0(i0), .i1(i1), .i2(i2), .i3(i3), .i4(i4), .i5(i5), .i6(i6), .i7(i7), .i8(i8), .i9(i9), .i10(i10),
    .i11(i11), .i12(i12), .i13(i13), .i14(i14), .i15(i15), .i0_2(i0_2), .i1_2(i1_2), .i2_2(i2_2),
    .i3_2(i3_2), .i4_2(i4_2), .i5_2(i5_2), .i6_2(i6_2), .i7_2(i7_2), .i8_2(i8_2), .i9_2(i9_2), .i10_2(i10_2),
    .i11_2(i11_2), .i12_2(i12_2), .i13_2(i13_2), .i14_2(i14_2), .i15_2(i15_2), .Y0(double16_1_y0),
    .Y1(double16_1_y1), .Y2(double16_1_y2), .Y3(double16_1_y3), .Y4(double16_1_y4), .Y5(double16_1_y5),
    .Y6(double16_1_y6), .Y7(double16_1_y7), .in_4(I0_3), .in_15(I1_3), .in_22(WI1), .in_23(I1en));
  RAM #(.addrWidth(8), .dataWidth(8), .bus("combined"), .Select("high")) ram_1 ();  // open: addr, data, sel, clk, ld, clr
  LED #(.active("true")) led_1 (.in(double16_1_y2));
  LED #(.active("true")) led_2 (.in(double16_1_y3));
  LED #(.active("true")) led_3 (.in(double16_1_y1));
  LED #(.active("true")) led_4 (.in(double16_1_y0));
  LED #(.active("true")) led_5 (.in(double16_1_y5));
  LED #(.active("true")) led_6 (.in(double16_1_y6));
  LED #(.active("true")) led_7 (.in(double16_1_y7));
  LED #(.active("true")) led_8 (.in(double16_1_y4));
  C8 u_Ain (
    .in_2(double16_1_y4), .in_3(double16_1_y5), .in_4(double16_1_y6), .in_5(double16_1_y7),
    .in_6(double16_1_y0), .in_7(double16_1_y1), .in_8(double16_1_y2), .in_9(double16_1_y3),
    .out_10(Ain_out_10), .out_11(Ain_out_11), .out_12(Ain_out_12), .out_13(Ain_out_13), .out_14(Ain_out_14),
    .out_15(Ain_out_15), .out_16(Ain_out_16), .out_17(Ain_out_17), .in_1(Ain));
  C8 u_Aout (
    .in_2(A_out_17), .in_3(A_out_16), .in_4(A_out_15), .in_5(A_out_14), .in_6(A_out_13), .in_7(A_out_12),
    .in_8(A_out_11), .in_9(A_out_10), .out_10(double16_1_y3), .out_11(double16_1_y2), .out_12(double16_1_y1),
    .out_13(double16_1_y0), .out_14(double16_1_y7), .out_15(double16_1_y6), .out_16(double16_1_y5),
    .out_17(double16_1_y4), .in_1(Aout));
  C8 c8_1 (
    .in_2(n8add_1_s0), .in_3(n8add_1_s1), .in_4(n8add_1_s2), .in_5(n8add_1_s3), .in_6(n8add_1_s4),
    .in_7(n8add_1_s5), .in_8(n8add_1_s6), .in_9(n8add_1_s7), .out_10(Ain_out_17), .out_11(Ain_out_16),
    .out_12(Ain_out_15), .out_13(Ain_out_14), .out_14(Ain_out_13), .out_15(Ain_out_12), .out_16(Ain_out_11),
    .out_17(Ain_out_10), .in_1(aout_2));
  _2seg u_2seg_1 (
    .i0(double16_1_y4), .i1(double16_1_y5), .i2(double16_1_y6), .i3(double16_1_y7), .i4(double16_1_y0),
    .i5(double16_1_y1), .i6(double16_1_y2), .i7(double16_1_y3), .out_10(n2seg_1_out_10),
    .out_11(n2seg_1_out_11), .out_12(n2seg_1_out_12), .out_13(n2seg_1_out_13), .out_14(n2seg_1_out_14),
    .out_15(n2seg_1_out_15), .out_16(n2seg_1_out_16), .out_17(n2seg_1_out_17), .out_18(n2seg_1_out_18),
    .out_19(n2seg_1_out_19), .out_20(n2seg_1_out_20), .out_21(n2seg_1_out_21), .out_22(n2seg_1_out_22),
    .out_23(n2seg_1_out_23), .in_2(O0));
  _8ADD u_8add_1 (
    .B7(C_out_10), .B6(C_out_11), .B5(C_out_12), .B3(C_out_14), .B2(C_out_15), .B1(C_out_16), .B0(C_out_17),
    .A7(B_out_10), .A6(B_out_11), .A5(B_out_12), .A4(B_out_13), .A3(B_out_14), .A2(B_out_15), .A1(B_out_16),
    .A0(B_out_17), .C(out_44), .S7(n8add_1_s7), .S6(n8add_1_s6), .S5(n8add_1_s5), .S4(n8add_1_s4),
    .S3(n8add_1_s3), .S2(n8add_1_s2), .S1(n8add_1_s1), .S0(n8add_1_s0), .B4(C_out_13));
  reg8 C (
    .out_10(C_out_10), .out_11(C_out_11), .out_12(C_out_12), .out_13(C_out_13), .out_14(C_out_14),
    .out_15(C_out_15), .out_16(C_out_16), .out_17(C_out_17), .in_2(A_out_10), .in_3(A_out_11),
    .in_4(A_out_12), .in_5(A_out_13), .in_6(A_out_14), .in_7(A_out_15), .in_8(A_out_16), .in_9(A_out_17),
    .in_1(Rt));
  reg8 A (
    .out_10(A_out_10), .out_11(A_out_11), .out_12(A_out_12), .out_13(A_out_13), .out_14(A_out_14),
    .out_15(A_out_15), .out_16(A_out_16), .out_17(A_out_17), .in_2(Ain_out_17), .in_3(Ain_out_16),
    .in_4(Ain_out_15), .in_5(Ain_out_14), .in_6(Ain_out_13), .in_7(Ain_out_12), .in_8(Ain_out_11),
    .in_9(Ain_out_10), .in_1(RA));
  reg8 B (
    .out_10(B_out_10), .out_11(B_out_11), .out_12(B_out_12), .out_13(B_out_13), .out_14(B_out_14),
    .out_15(B_out_15), .out_16(B_out_16), .out_17(B_out_17), .in_2(A_out_10), .in_3(A_out_11),
    .in_4(A_out_12), .in_5(A_out_13), .in_6(A_out_14), .in_7(A_out_15), .in_8(A_out_16), .in_9(A_out_17),
    .in_1(RB));
  _7_Segment_Display #(.active("false")) u_7_segment_display_1 (
    .g(n2seg_1_out_23), .f(n2seg_1_out_22), .a(n2seg_1_out_17), .b(n2seg_1_out_18), .e(n2seg_1_out_21),
    .d(n2seg_1_out_20), .c(n2seg_1_out_19), .dp(1'b1));
  _7_Segment_Display #(.active("false")) u_7_segment_display_2 (
    .g(n2seg_1_out_16), .f(n2seg_1_out_15), .a(n2seg_1_out_10), .b(n2seg_1_out_11), .e(n2seg_1_out_14),
    .d(n2seg_1_out_13), .c(n2seg_1_out_12), .dp(1'b1));
endmodule

module HA (
  input  \加数 ,
  input  \加数_2 ,
  output \个位 ,
  output \十位 
);

  xor xor_1 (\个位 , \加数 , \加数_2 );
  and and_1 (\十位 , \加数 , \加数_2 );
endmodule

module FA (
  input  \前一次运算的进位 ,
  input  \加数 ,
  input  \加数_2 ,
  output \和 ,
  output \运算产生的进位 
);

  wire \ha_1_个位 , \ha_1_十位 , \ha_2_十位 ;

  HA ha_1 (.\加数 (\加数 ), .\加数_2 (\加数_2 ), .\个位 (\ha_1_个位 ), .\十位 (\ha_1_十位 ));
  HA ha_2 (.\加数 (\前一次运算的进位 ), .\加数_2 (\ha_1_个位 ), .\个位 (\和 ), .\十位 (\ha_2_十位 ));
  or or_1 (\运算产生的进位 , \ha_2_十位 , \ha_1_十位 );
endmodule

module _8ADD (
  input  B7,
  input  B6,
  input  B5,
  input  B4,
  input  B3,
  input  B2,
  input  B1,
  input  B0,
  input  A7,
  input  A6,
  input  A5,
  input  A4,
  input  A3,
  input  A2,
  input  A1,
  input  A0,
  output C,
  output S7,
  output S6,
  output S5,
  output S4,
  output S3,
  output S2,
  output S1,
  output S0
);

  wire \fa_1_运算产生的进位 , \fa_2_运算产生的进位 , \fa_3_运算产生的进位 , \fa_4_运算产生的进位 , \fa_5_运算产生的进位 , \fa_6_运算产生的进位 ,
       \fa_7_运算产生的进位 ;

  FA fa_1 (.\前一次运算的进位 (1'b0), .\加数 (B0), .\加数_2 (A0), .\和 (S0), .\运算产生的进位 (\fa_1_运算产生的进位 ));
  FA fa_2 (.\前一次运算的进位 (\fa_1_运算产生的进位 ), .\加数 (B1), .\加数_2 (A1), .\和 (S1), .\运算产生的进位 (\fa_2_运算产生的进位 ));
  FA fa_3 (.\前一次运算的进位 (\fa_2_运算产生的进位 ), .\加数 (B2), .\加数_2 (A2), .\和 (S2), .\运算产生的进位 (\fa_3_运算产生的进位 ));
  FA fa_4 (.\前一次运算的进位 (\fa_3_运算产生的进位 ), .\加数 (B3), .\加数_2 (A3), .\和 (S3), .\运算产生的进位 (\fa_4_运算产生的进位 ));
  FA fa_5 (.\前一次运算的进位 (\fa_4_运算产生的进位 ), .\加数 (B4), .\加数_2 (A4), .\和 (S4), .\运算产生的进位 (\fa_5_运算产生的进位 ));
  FA fa_6 (.\前一次运算的进位 (\fa_5_运算产生的进位 ), .\加数 (B5), .\加数_2 (A5), .\和 (S5), .\运算产生的进位 (\fa_6_运算产生的进位 ));
  FA fa_7 (.\前一次运算的进位 (\fa_6_运算产生的进位 ), .\加数 (B6), .\加数_2 (A6), .\和 (S6), .\运算产生的进位 (\fa_7_运算产生的进位 ));
  FA fa_8 (.\前一次运算的进位 (\fa_7_运算产生的进位 ), .\加数 (B7), .\加数_2 (A7), .\和 (S7), .\运算产生的进位 (C));
endmodule

module add1 (
  input  \乘数 ,
  input  \上一运算的进位 ,
  input  \乘数_2 ,
  input  \上一运算的积 ,
  input  in_5,
  input  in_6,
  input  in_7,
  input  in_8,
  input  in_9,
  input  in_10,
  output \积 ,
  output out_12,
  output out_13,
  output out_14,
  output out_15
);

  wire and_1_out, and_2_out, and_3_out, and_4_out, \fa_1_运算产生的进位 , \fa_2_运算产生的进位 , \fa_3_运算产生的进位 ;

  and and_1 (and_1_out, \乘数 , \乘数_2 );
  and and_2 (and_2_out, \乘数 , in_5);
  and and_3 (and_3_out, \乘数 , in_7);
  and and_4 (and_4_out, \乘数 , in_9);
  FA fa_1 (.\前一次运算的进位 (\上一运算的进位 ), .\加数 (and_1_out), .\加数_2 (\上一运算的积 ), .\和 (\积 ), .\运算产生的进位 (\fa_1_运算产生的进位 ));
  FA fa_2 (.\前一次运算的进位 (\fa_1_运算产生的进位 ), .\加数 (and_2_out), .\加数_2 (in_6), .\和 (out_12), .\运算产生的进位 (\fa_2_运算产生的进位 ));
  FA fa_3 (.\前一次运算的进位 (\fa_2_运算产生的进位 ), .\加数 (and_3_out), .\加数_2 (in_8), .\和 (out_13), .\运算产生的进位 (\fa_3_运算产生的进位 ));
  FA fa_4 (.\前一次运算的进位 (\fa_3_运算产生的进位 ), .\加数 (and_4_out), .\加数_2 (in_10), .\和 (out_14), .\运算产生的进位 (out_15));

  // Notes on the sheet:
  //   进位
endmodule

module \乘法器  (
  input  in_1,
  input  in_2,
  input  in_3,
  input  in_4,
  input  in_5,
  input  in_6,
  input  in_7,
  input  in_8,
  input  in_9,
  output out_10,
  output out_11,
  output out_12,
  output out_13,
  output out_14,
  output out_15,
  output out_16,
  output out_17
);

  wire add1_1_out_12, add1_1_out_13, add1_1_out_14, add1_1_out_15, add1_2_out_12, add1_2_out_13,
       add1_2_out_14, add1_2_out_15, add1_3_out_12, add1_3_out_13, add1_3_out_14, add1_3_out_15, and_1_out,
       and_2_out, and_3_out, and_4_out, and_5_out, and_6_out, and_7_out, and_8_out;

  and and_1 (and_1_out, in_5, in_9);
  and and_2 (and_2_out, in_6, in_9);
  and and_3 (and_3_out, in_7, in_9);
  and and_4 (and_4_out, in_8, in_9);
  and and_5 (and_5_out, in_1, in_9);
  add1 add1_1 (
    .\乘数_2 (and_1_out), .\上一运算的积 (1'b0), .in_5(and_2_out), .in_6(1'b0), .in_7(and_3_out), .in_8(1'b0),
    .in_9(and_4_out), .in_10(1'b0), .\乘数 (and_5_out), .\上一运算的进位 (1'b0), .\积 (out_10), .out_12(add1_1_out_12),
    .out_13(add1_1_out_13), .out_14(add1_1_out_14), .out_15(add1_1_out_15));
  and and_6 (and_6_out, in_2, in_9);
  add1 add1_2 (
    .\乘数_2 (and_1_out), .\上一运算的积 (add1_1_out_12), .in_5(and_2_out), .in_6(add1_1_out_13), .in_7(and_3_out),
    .in_8(add1_1_out_14), .in_9(and_4_out), .in_10(add1_1_out_15), .\乘数 (and_6_out), .\上一运算的进位 (1'b0),
    .\积 (out_11), .out_12(add1_2_out_12), .out_13(add1_2_out_13), .out_14(add1_2_out_14),
    .out_15(add1_2_out_15));
  and and_7 (and_7_out, in_3, in_9);
  add1 add1_3 (
    .\乘数_2 (and_1_out), .\上一运算的积 (add1_2_out_12), .in_5(and_2_out), .in_6(add1_2_out_13), .in_7(and_3_out),
    .in_8(add1_2_out_14), .in_9(and_4_out), .in_10(add1_2_out_15), .\乘数 (and_7_out), .\上一运算的进位 (1'b0),
    .\积 (out_12), .out_12(add1_3_out_12), .out_13(add1_3_out_13), .out_14(add1_3_out_14),
    .out_15(add1_3_out_15));
  and and_8 (and_8_out, in_4, in_9);
  add1 add1_4 (
    .\乘数_2 (and_1_out), .\上一运算的积 (add1_3_out_12), .in_5(and_2_out), .in_6(add1_3_out_13), .in_7(and_3_out),
    .in_8(add1_3_out_14), .in_9(and_4_out), .in_10(add1_3_out_15), .\乘数 (and_8_out), .\上一运算的进位 (1'b0),
    .\积 (out_13), .out_12(out_14), .out_13(out_15), .out_14(out_16), .out_15(out_17));
endmodule

module \做乘法  (
  input  in_1,
  input  \高位 ,
  input  in_3,
  input  in_4,
  input  in_5,
  input  \低位 ,
  input  in_7,
  input  in_8,
  input  in_9,
  output out_10,
  output out_11,
  output out_12,
  output out_13,
  output out_14,
  output out_15,
  output out_16,
  output out_17
);

  wire n2seg_1_out_10, n2seg_1_out_11, n2seg_1_out_12, n2seg_1_out_13, n2seg_1_out_14, n2seg_1_out_15,
       n2seg_1_out_16, n2seg_1_out_17, n2seg_1_out_18, n2seg_1_out_19, n2seg_1_out_20, n2seg_1_out_21,
       n2seg_1_out_22, n2seg_1_out_23;

  LED #(.active("true")) led_1 (.in(\低位 ));
  LED #(.active("true")) led_2 (.in(in_7));
  LED #(.active("true")) led_3 (.in(in_8));
  LED #(.active("true")) led_4 (.in(in_5));
  LED #(.active("true")) led_5 (.in(in_4));
  LED #(.active("true")) led_6 (.in(in_1));
  LED #(.active("true")) led_7 (.in(in_3));
  LED #(.active("true")) led_8 (.in(\高位 ));
  \乘法器  \u_乘法器_1  (
    .in_5(in_5), .in_6(\低位 ), .in_7(in_7), .in_8(in_8), .out_10(out_17), .out_11(out_16), .out_12(out_15),
    .out_13(out_14), .out_14(out_13), .out_15(out_12), .out_16(out_11), .out_17(out_10), .in_1(in_1),
    .in_2(\高位 ), .in_3(in_3), .in_4(in_4), .in_9(in_9));
  _2seg u_2seg_1 (
    .i0(out_17), .i1(out_16), .i2(out_15), .i3(out_14), .i4(out_13), .i5(out_12), .i6(out_11), .i7(out_10),
    .out_10(n2seg_1_out_10), .out_11(n2seg_1_out_11), .out_12(n2seg_1_out_12), .out_13(n2seg_1_out_13),
    .out_14(n2seg_1_out_14), .out_15(n2seg_1_out_15), .out_16(n2seg_1_out_16), .out_17(n2seg_1_out_17),
    .out_18(n2seg_1_out_18), .out_19(n2seg_1_out_19), .out_20(n2seg_1_out_20), .out_21(n2seg_1_out_21),
    .out_22(n2seg_1_out_22), .out_23(n2seg_1_out_23), .in_2(in_9));
  _7_Segment_Display #(.active("false")) u_7_segment_display_1 (
    .g(n2seg_1_out_23), .f(n2seg_1_out_22), .a(n2seg_1_out_17), .b(n2seg_1_out_18), .e(n2seg_1_out_21),
    .d(n2seg_1_out_20), .c(n2seg_1_out_19), .dp(1'b1));
  _7_Segment_Display #(.active("false")) u_7_segment_display_2 (
    .g(n2seg_1_out_16), .f(n2seg_1_out_15), .a(n2seg_1_out_10), .b(n2seg_1_out_11), .e(n2seg_1_out_14),
    .d(n2seg_1_out_13), .c(n2seg_1_out_12), .dp(1'b1));

  // Notes on the sheet:
  //   结果
  //   十六进制输出
endmodule
