// Logisim project 程序存储冯诺依曼计算机.circ as structural Verilog: 4 circuits, main circuit main
module main (
  input  i0,
  input  i1,
  input  i2,
  input  i3,
  input  i4,
  input  i5,
  input  i6,
  input  i7,
  input  i8,
  input  i9,
  input  i10,
  input  i11,
  input  i12,
  input  i13,
  input  i14,
  input  i15,
  input  i0_2,
  input  i1_2,
  input  i2_2,
  input  i3_2,
  input  i4_2,
  input  i5_2,
  input  i6_2,
  input  i7_2,
  input  i8_2,
  input  i9_2,
  input  i10_2,
  input  i11_2,
  input  i12_2,
  input  i13_2,
  input  i14_2,
  input  i15_2,
  input  WI1,
  input  I1en,
  output out_35
);

  wire Ain_out_10, Ain_out_11, Ain_out_12, Ain_out_13, Ain_out_14, Ain_out_15, Ain_out_16, Ain_out_17,
       clock_1_out, double16_1_y0, double16_1_y1, double16_1_y2, double16_1_y3, double16_1_y4, double16_1_y5,
       double16_1_y6, double16_1_y7, n2seg_1_out_10, n2seg_1_out_11, n2seg_1_out_12, n2seg_1_out_13,
       n2seg_1_out_14, n2seg_1_out_15, n2seg_1_out_16, n2seg_1_out_17, n2seg_1_out_18, n2seg_1_out_19,
       n2seg_1_out_20, n2seg_1_out_21, n2seg_1_out_22, n2seg_1_out_23, n8add_1_s0, n8add_1_s1, n8add_1_s2,
       n8add_1_s3, n8add_1_s4, n8add_1_s5, n8add_1_s6, n8add_1_s7, reg8_1_out_10, reg8_1_out_11,
       reg8_1_out_12, reg8_1_out_13, reg8_1_out_14, reg8_1_out_15, reg8_1_out_16, reg8_1_out_17,
       reg8_2_out_10, reg8_2_out_11, reg8_2_out_12, reg8_2_out_13, reg8_2_out_14, reg8_2_out_15,
       reg8_2_out_16, reg8_2_out_17, reg8_3_out_10, reg8_3_out_11, reg8_3_out_12, reg8_3_out_13,
       reg8_3_out_14, reg8_3_out_15, reg8_3_out_16, reg8_3_out_17;
  wire [3:0] counter_1_q;
  wire [8:0] rom_1_data;

  double16 double16_1 (
    .i0(i0), .i1(i1), .i2(i2), .i3(i3), .i4(i4), .i5(i5), .i6(i6), .i7(i7), .i8(i8), .i9(i9), .i10(i10),
    .i11(i11), .i12(i12), .i13(i13), .i14(i14), .i15(i15), .i0_2(i0_2), .i1_2(i1_2), .i2_2(i2_2),
    .i3_2(i3_2), .i4_2(i4_2), .i5_2(i5_2), .i6_2(i6_2), .i7_2(i7_2), .i8_2(i8_2), .i9_2(i9_2), .i10_2(i10_2),
    .i11_2(i11_2), .i12_2(i12_2), .i13_2(i13_2), .i14_2(i14_2), .i15_2(i15_2), .Y0(double16_1_y0),
    .Y1(double16_1_y1), .Y2(double16_1_y2), .Y3(double16_1_y3), .Y4(double16_1_y4), .Y5(double16_1_y5),
    .Y6(double16_1_y6), .Y7(double16_1_y7), .in_4(rom_1_data[8]), .in_15(rom_1_data[7]), .in_22(WI1),
    .in_23(I1en));
  LED #(.active("true")) led_1 (.in(double16_1_y3));
  LED #(.active("true")) led_2 (.in(double16_1_y2));
  LED #(.active("true")) led_3 (.in(double16_1_y1));
  LED #(.active("true")) led_4 (.in(double16_1_y0));
  LED #(.active("true")) led_5 (.in(double16_1_y7));
  LED #(.active("true")) led_6 (.in(double16_1_y6));
  LED #(.active("true")) led_7 (.in(double16_1_y5));
  LED #(.active("true")) led_8 (.in(double16_1_y4));
  C8 Ain (
    .in_2(double16_1_y4), .in_3(double16_1_y5), .in_4(double16_1_y6), .in_5(double16_1_y7),
    .in_6(double16_1_y0), .in_7(double16_1_y1), .in_8(double16_1_y2), .in_9(double16_1_y3),
    .out_10(Ain_out_10), .out_11(Ain_out_11), .out_12(Ain_out_12), .out_13(Ain_out_13), .out_14(Ain_out_14),
    .out_15(Ain_out_15), .out_16(Ain_out_16), .out_17(Ain_out_17), .in_1(rom_1_data[6]));
  C8 c8_1 (
    .in_2(n8add_1_s0), .in_3(n8add_1_s1), .in_4(n8add_1_s2), .in_5(n8add_1_s3), .in_6(n8add_1_s4),
    .in_7(n8add_1_s5), .in_8(n8add_1_s6), .in_9(n8add_1_s7), .out_10(Ain_out_17), .out_11(Ain_out_16),
    .out_12(Ain_out_15), .out_13(Ain_out_14), .out_14(Ain_out_13), .out_15(Ain_out_12), .out_16(Ain_out_11),
    .out_17(Ain_out_10), .in_1(rom_1_data[4]));
  C8 Aout (
    .in_2(reg8_2_out_17), .in_3(reg8_2_out_16), .in_4(reg8_2_out_15), .in_5(reg8_2_out_14),
    .in_6(reg8_2_out_13), .in_7(reg8_2_out_12), .in_8(reg8_2_out_11), .in_9(reg8_2_out_10),
    .out_10(double16_1_y3), .out_11(double16_1_y2), .out_12(double16_1_y1), .out_13(double16_1_y0),
    .out_14(double16_1_y7), .out_15(double16_1_y6), .out_16(double16_1_y5), .out_17(double16_1_y4),
    .in_1(rom_1_data[5]));
  _8ADD u_8add_1 (
    .B7(reg8_1_out_10), .B6(reg8_1_out_11), .B5(reg8_1_out_12), .B4(reg8_1_out_13), .B3(reg8_1_out_14),
    .B2(reg8_1_out_15), .B1(reg8_1_out_16), .B0(reg8_1_out_17), .A7(reg8_3_out_10), .A6(reg8_3_out_11),
    .A5(reg8_3_out_12), .A4(reg8_3_out_13), .A3(reg8_3_out_14), .A2(reg8_3_out_15), .A1(reg8_3_out_16),
    .A0(reg8_3_out_17), .C(out_35), .S7(n8add_1_s7), .S6(n8add_1_s6), .S5(n8add_1_s5), .S4(n8add_1_s4),
    .S3(n8add_1_s3), .S2(n8add_1_s2), .S1(n8add_1_s1), .S0(n8add_1_s0));
  reg8 reg8_1 (
    .out_10(reg8_1_out_10), .out_11(reg8_1_out_11), .out_12(reg8_1_out_12), .out_13(reg8_1_out_13),
    .out_14(reg8_1_out_14), .out_15(reg8_1_out_15), .out_16(reg8_1_out_16), .out_17(reg8_1_out_17),
    .in_2(reg8_2_out_10), .in_3(reg8_2_out_11), .in_4(reg8_2_out_12), .in_5(reg8_2_out_13),
    .in_6(reg8_2_out_14), .in_7(reg8_2_out_15), .in_8(reg8_2_out_16), .in_9(reg8_2_out_17),
    .in_1(rom_1_data[2]));
  reg8 reg8_2 (
    .out_10(reg8_2_out_10), .out_11(reg8_2_out_11), .out_12(reg8_2_out_12), .out_13(reg8_2_out_13),
    .out_14(reg8_2_out_14), .out_15(reg8_2_out_15), .out_16(reg8_2_out_16), .out_17(reg8_2_out_17),
    .in_2(Ain_out_17), .in_3(Ain_out_16), .in_4(Ain_out_15), .in_5(Ain_out_14), .in_6(Ain_out_13),
    .in_7(Ain_out_12), .in_8(Ain_out_11), .in_9(Ain_out_10), .in_1(rom_1_data[3]));
  reg8 reg8_3 (
    .out_10(reg8_3_out_10), .out_11(reg8_3_out_11), .out_12(reg8_3_out_12), .out_13(reg8_3_out_13),
    .out_14(reg8_3_out_14), .out_15(reg8_3_out_15), .out_16(reg8_3_out_16), .out_17(reg8_3_out_17),
    .in_2(reg8_2_out_10), .in_3(reg8_2_out_11), .in_4(reg8_2_out_12), .in_5(reg8_2_out_13),
    .in_6(reg8_2_out_14), .in_7(reg8_2_out_15), .in_8(reg8_2_out_16), .in_9(reg8_2_out_17),
    .in_1(rom_1_data[1]));
  _2seg u_2seg_1 (
    .i0(double16_1_y4), .i1(double16_1_y5), .i2(double16_1_y6), .i3(double16_1_y7), .i4(double16_1_y0),
    .i5(double16_1_y1), .i6(double16_1_y2), .i7(double16_1_y3), .out_10(n2seg_1_out_10),
    .out_11(n2seg_1_out_11), .out_12(n2seg_1_out_12), .out_13(n2seg_1_out_13), .out_14(n2seg_1_out_14),
    .out_15(n2seg_1_out_15), .out_16(n2seg_1_out_16), .out_17(n2seg_1_out_17), .out_18(n2seg_1_out_18),
    .out_19(n2seg_1_out_19), .out_20(n2seg_1_out_20), .out_21(n2seg_1_out_21), .out_22(n2seg_1_out_22),
    .out_23(n2seg_1_out_23), .in_2(rom_1_data[0]));
  Counter #(.width(4), .max('hf), .ongoal("wrap"), .trigger("rising"), .behavior("old")) counter_1 (
    .Q(counter_1_q), .clk(clock_1_out));  // open: load, D, count, carry, clr, preset
  Clock #(.highDuration(1), .lowDuration(1)) clock_1 (.out(clock_1_out));
  _7_Segment_Display #(.active("false")) u_7_segment_display_1 (
    .g(n2seg_1_out_23), .f(n2seg_1_out_22), .a(n2seg_1_out_17), .b(n2seg_1_out_18), .e(n2seg_1_out_21),
    .d(n2seg_1_out_20), .c(n2seg_1_out_19), .dp(1'b1));
  ROM #(.addrWidth(4), .dataWidth(9), .Select("high")) rom_1 (.addr(counter_1_q), .data(rom_1_data));
  _7_Segment_Display #(.active("false")) u_7_segment_display_2 (
    .g(n2seg_1_out_16), .f(n2seg_1_out_15), .a(n2seg_1_out_10), .b(n2seg_1_out_11), .e(n2seg_1_out_14),
    .d(n2seg_1_out_13), .c(n2seg_1_out_12), .dp(1'b1));

  // Notes on the sheet:
  //   contents of rom_1 (hex, n*v repeats v):
  //   101 149 141 3 1 81 c1 c9 c1 5 11 19 11 21
endmodule

module HA (
  input  Bi,
  input  Ai,
  output Si,
  output Ci_1
);

  xor xor_1 (Si, Bi, Ai);
  and and_1 (Ci_1, Bi, Ai);
endmodule

module FA (
  input  Cn_1,
  input  Bn,
  input  An,
  output Sn,
  output Cn
);

  wire ha_1_ci_1, ha_1_si, ha_2_ci_1;

  HA ha_1 (.Bi(Bn), .Ai(An), .Si(ha_1_si), .Ci_1(ha_1_ci_1));
  HA ha_2 (.Bi(Cn_1), .Ai(ha_1_si), .Si(Sn), .Ci_1(ha_2_ci_1));
  or or_1 (Cn, ha_2_ci_1, ha_1_ci_1);
endmodule

module _8ADD (
  input  B7,
  input  B6,
  input  B5,
  input  B4,
  input  B3,
  input  B2,
  input  B1,
  input  B0,
  input  A7,
  input  A6,
  input  A5,
  input  A4,
  input  A3,
  input  A2,
  input  A1,
  input  A0,
  output C,
  output S7,
  output S6,
  output S5,
  output S4,
  output S3,
  output S2,
  output S1,
  output S0
);

  wire fa_1_cn, fa_2_cn, fa_3_cn, fa_4_cn, fa_5_cn, fa_6_cn, fa_7_cn;

  FA fa_1 (.Cn_1(1'b0), .Bn(B0), .An(A0), .Sn(S0), .Cn(fa_1_cn));
  FA fa_2 (.Cn_1(fa_1_cn), .Bn(B1), .An(A1), .Sn(S1), .Cn(fa_2_cn));
  FA fa_3 (.Cn_1(fa_2_cn), .Bn(B2), .An(A2), .Sn(S2), .Cn(fa_3_cn));
  FA fa_4 (.Cn_1(fa_3_cn), .Bn(B3), .An(A3), .Sn(S3), .Cn(fa_4_cn));
  FA fa_5 (.Cn_1(fa_4_cn), .Bn(B4), .An(A4), .Sn(S4), .Cn(fa_5_cn));
  FA fa_6 (.Cn_1(fa_5_cn), .Bn(B5), .An(A5), .Sn(S5), .Cn(fa_6_cn));
  FA fa_7 (.Cn_1(fa_6_cn), .Bn(B6), .An(A6), .Sn(S6), .Cn(fa_7_cn));
  FA fa_8 (.Cn_1(fa_7_cn), .Bn(B7), .An(A7), .Sn(S7), .Cn(C));
endmodule
