// Logisim project BCD七段数码管.circ as structural Verilog: 9 circuits, main circuit a
module main (
  input  A,
  input  B,
  input  C,
  input  D
);

  wire seg_1_out_5, seg_1_out_6, seg_1_out_7, seg_1_out_8, seg_1_out_9, seg_1_out_10, seg_1_out_11;

  seg seg_1 (
    .A(A), .B(B), .C(C), .D(D), .out_5(seg_1_out_5), .out_6(seg_1_out_6), .out_7(seg_1_out_7),
    .out_8(seg_1_out_8), .out_9(seg_1_out_9), .out_10(seg_1_out_10), .out_11(seg_1_out_11));
  _7_Segment_Display u_7_segment_display_1 (
    .g(seg_1_out_11), .f(seg_1_out_10), .a(seg_1_out_5), .b(seg_1_out_6), .e(seg_1_out_9), .d(seg_1_out_8),
    .c(seg_1_out_7), .dp(1'b0));
endmodule

// A
module a (
  input  A,
  input  B,
  input  C,
  input  D,
  output a_2
);

  wire and_1_out, and_2_out, not_1_out, not_2_out;

  not not_1 (not_1_out, B);
  and and_1 (and_1_out, not_1_out, not_2_out);
  not not_2 (not_2_out, D);
  and and_2 (and_2_out, B, D);
  or or_1 (a_2, and_1_out, C, and_2_out, A);
endmodule

module b (
  input  A,
  input  B,
  input  C,
  input  D,
  output b_2
);

  wire and_1_out, and_2_out, not_1_out, not_2_out, not_3_out;

  not not_1 (not_1_out, B);
  not not_2 (not_2_out, C);
  and and_1 (and_1_out, not_2_out, not_3_out);
  not not_3 (not_3_out, D);
  and and_2 (and_2_out, C, D);
  or or_1 (b_2, not_1_out, and_1_out, and_2_out);
endmodule

module c (
  input  A,
  input  B,
  input  C,
  input  D,
  output c_2
);

  wire not_1_out;

  not not_1 (not_1_out, C);
  or or_1 (c_2, not_1_out, D, B);
endmodule

module d (
  input  A,
  input  B,
  input  C,
  input  D,
  output d_2
);

  wire and_1_out, and_2_out, and_3_out, and_4_out, not_1_out, not_2_out, not_3_out, not_4_out, not_5_out;

  not not_1 (not_1_out, B);
  and and_1 (and_1_out, not_1_out, not_2_out);
  not not_2 (not_2_out, D);
  not not_3 (not_3_out, B);
  and and_2 (and_2_out, not_3_out, C);
  and and_3 (and_3_out, C, not_4_out);
  not not_4 (not_4_out, D);
  not not_5 (not_5_out, C);
  and and_4 (and_4_out, B, not_5_out, D);
  or or_1 (d_2, and_1_out, and_2_out, and_3_out, and_4_out, A);
endmodule

module e (
  input  A,
  input  B,
  input  C,
  input  D,
  output e
);

  wire and_1_out, and_2_out, not_1_out, not_2_out, not_3_out;

  not not_1 (not_1_out, B);
  and and_1 (and_1_out, not_1_out, not_2_out);
  not not_2 (not_2_out, D);
  and and_2 (and_2_out, C, not_3_out);
  not not_3 (not_3_out, D);
  or or_1 (e, and_1_out, and_2_out);
endmodule

module f (
  input  A,
  input  B,
  input  C,
  input  D,
  output f
);

  wire and_1_out, and_2_out, and_3_out, not_1_out, not_2_out, not_3_out, not_4_out;

  not not_1 (not_1_out, C);
  and and_1 (and_1_out, not_1_out, not_2_out);
  not not_2 (not_2_out, D);
  and and_2 (and_2_out, B, not_3_out);
  not not_3 (not_3_out, C);
  and and_3 (and_3_out, B, not_4_out);
  not not_4 (not_4_out, D);
  or or_1 (f, and_1_out, and_2_out, and_3_out, A);
endmodule

module g (
  input  A,
  input  B,
  input  C,
  input  D,
  output g
);

  wire and_1_out, and_2_out, and_3_out, not_1_out, not_2_out, not_3_out;

  not not_1 (not_1_out, B);
  and and_1 (and_1_out, not_1_out, C);
  and and_2 (and_2_out, B, not_2_out);
  not not_2 (not_2_out, C);
  and and_3 (and_3_out, B, not_3_out);
  not not_3 (not_3_out, D);
  or or_1 (g, and_1_out, and_2_out, and_3_out, A);
endmodule

module seg (
  input  A,
  input  B,
  input  C,
  input  D,
  output out_5,
  output out_6,
  output out_7,
  output out_8,
  output out_9,
  output out_10,
  output out_11
);

  a a_1 (.A(A), .B(B), .C(C), .D(D), .a_2(out_5));
  b b_1 (.A(A), .B(B), .C(C), .D(D), .b_2(out_6));
  c c_1 (.A(A), .B(B), .C(C), .D(D), .c_2(out_7));
  d d_1 (.A(A), .B(B), .C(C), .D(D), .d_2(out_8));
  e e_1 (.A(A), .B(B), .C(C), .D(D), .e(out_9));
  f f_1 (.A(A), .B(B), .C(C), .D(D), .f(out_10));
  g g_1 (.A(A), .B(B), .C(C), .D(D), .g(out_11));
endmodule
