// Logisim project 11带数码管输出4_计数器离开总线coreArith21.circ as structural Verilog: 27 circuits, main circuit main
module main (
  input  i0,
  input  i1,
  input  i2,
  input  i3,
  input  i4,
  input  i5,
  input  i6,
  input  i7,
  input  i8,
  input  i9,
  input  iA,
  input  iB,
  input  iC,
  input  iD,
  input  iE,
  input  iF,
  input  i0_2,
  input  i1_2,
  input  i2_2,
  input  i3_2,
  input  i4_2,
  input  i5_2,
  input  i6_2,
  input  i7_2,
  input  i8_2,
  input  i9_2,
  input  iA_2,
  input  iB_2,
  input  iC_2,
  input  iD_2,
  input  iE_2,
  input  in_32,
  input  iF_2,
  input  \自动_手动 ,
  input  in_35,
  input  KEY,
  input  KEY_2,
  input  R0,
  input  Rd,
  input  R1,
  input  in_41,
  input  i7_3
);

  wire Ain_out_16, Ain_out_17, clock_1_out, cs2_1_out_22, cs2_1_out_23, cs2_1_out_24, cs2_1_out_25,
       cs2_1_out_27, cs2_1_out_28, cs2_1_out_29, cs2_1_out_30, reg8_1_out_10, reg8_1_out_11, reg8_1_out_12,
       reg8_1_out_13, reg8_1_out_14, reg8_1_out_15, reg8_1_out_16, reg8_1_out_17, reg8_2_out_10,
       reg8_2_out_11, reg8_2_out_12, reg8_2_out_13, reg8_2_out_14, reg8_2_out_15, reg8_2_out_16,
       reg8_2_out_17, seg2_1_out_10, seg2_1_out_11, seg2_1_out_12, seg2_1_out_13, seg2_1_out_14,
       seg2_1_out_15, seg2_1_out_16, seg2_1_out_17, seg2_1_out_18, seg2_1_out_19, seg2_1_out_20,
       seg2_1_out_21, seg2_1_out_22, seg2_1_out_23;
  wire [5:0] Ain_out_10;
  wire [5:2] counter_1_q;
  wire [7:0] key_16_1_y0, ram_1_data;
  wire [8:0] rom_2_data;
  wire [9:0] counter_1_q_2;

  key_16 key_16_1 (
    .i0(i0), .i1(i1), .i2(i2), .i3(i3), .i4(i4), .i5(i5), .i6(i6), .i7(i7), .i0_2(i8), .i1_2(i9), .i2_2(iA),
    .i3_2(iB), .i4_2(iC), .i5_2(iD), .i6_2(iE), .i7_2(iF), .i0_3(i0_2), .i1_3(i1_2), .i2_3(i2_2),
    .i3_3(i3_2), .i4_3(i4_2), .i5_3(i5_2), .i6_3(i6_2), .i7_3(i7_2), .i0_4(i8_2), .i1_4(i9_2), .i2_4(iA_2),
    .i3_4(iB_2), .i4_4(iC_2), .i5_4(iD_2), .i6_4(iE_2), .i7_4(iF_2), .in_13(cs2_1_out_24),
    .y0(key_16_1_y0[0]), .y1(key_16_1_y0[1]), .y2(key_16_1_y0[2]), .y3(key_16_1_y0[3]),
    .y0_2(key_16_1_y0[4]), .y1_2(key_16_1_y0[5]), .y2_2(key_16_1_y0[6]), .y3_2(key_16_1_y0[7]));
  RAM #(.addrWidth(4)) ram_1 (.data(ram_1_data), .sel(in_32));  // open: addr, clk, ld, clr
  ROM #(.addrWidth(4)) rom_1 (.addr(counter_1_q), .data(key_16_1_y0), .sel(counter_1_q_2[1]));
  c8 Ain (
    .in_1(cs2_1_out_23), .out_10(Ain_out_10[0]), .out_11(Ain_out_10[1]), .out_12(Ain_out_10[2]),
    .out_13(Ain_out_10[3]), .out_14(Ain_out_10[4]), .out_15(Ain_out_10[5]), .out_16(Ain_out_16),
    .out_17(Ain_out_17), .in_2(key_16_1_y0[7]), .in_3(key_16_1_y0[6]), .in_4(key_16_1_y0[5]),
    .in_5(key_16_1_y0[4]), .in_6(key_16_1_y0[3]), .in_7(key_16_1_y0[2]), .in_8(key_16_1_y0[1]),
    .in_9(key_16_1_y0[0]));
  c8 Aout (
    .in_1(cs2_1_out_30), .out_10(key_16_1_y0[0]), .out_11(key_16_1_y0[1]), .out_12(key_16_1_y0[2]),
    .out_13(key_16_1_y0[3]), .out_14(key_16_1_y0[4]), .out_15(key_16_1_y0[5]), .out_16(key_16_1_y0[6]),
    .out_17(key_16_1_y0[7]), .in_2(reg8_1_out_17), .in_3(reg8_1_out_16), .in_4(reg8_1_out_15),
    .in_5(reg8_1_out_14), .in_6(reg8_1_out_13), .in_7(reg8_1_out_12), .in_8(reg8_1_out_11),
    .in_9(reg8_1_out_10));
  seg2 seg2_1 (
    .i0(key_16_1_y0[0]), .i1(key_16_1_y0[1]), .i2(key_16_1_y0[2]), .i3(key_16_1_y0[3]), .i4(key_16_1_y0[4]),
    .i5(key_16_1_y0[5]), .i6(key_16_1_y0[6]), .i7(key_16_1_y0[7]), .in_1(cs2_1_out_22),
    .out_10(seg2_1_out_10), .out_11(seg2_1_out_11), .out_12(seg2_1_out_12), .out_13(seg2_1_out_13),
    .out_14(seg2_1_out_14), .out_15(seg2_1_out_15), .out_16(seg2_1_out_16), .out_17(seg2_1_out_17),
    .out_18(seg2_1_out_18), .out_19(seg2_1_out_19), .out_20(seg2_1_out_20), .out_21(seg2_1_out_21),
    .out_22(seg2_1_out_22), .out_23(seg2_1_out_23));
  reg8 reg8_1 (
    .out_10(reg8_1_out_10), .out_11(reg8_1_out_11), .out_12(reg8_1_out_12), .out_13(reg8_1_out_13),
    .out_14(reg8_1_out_14), .out_15(reg8_1_out_15), .out_16(reg8_1_out_16), .out_17(reg8_1_out_17),
    .in_2(Ain_out_17), .in_3(Ain_out_16), .in_4(Ain_out_10[5]), .in_5(Ain_out_10[4]), .in_6(Ain_out_10[3]),
    .in_7(Ain_out_10[2]), .in_8(Ain_out_10[1]), .in_9(Ain_out_10[0]), .in_1(cs2_1_out_25));
  CS2 cs2_1 (
    .SEG(in_35), .KEY(KEY), .KEY_3(KEY_2), .R0(R0), .Rd(Rd), .R1(R1), .in_14(in_41), .out_22(cs2_1_out_22),
    .out_23(cs2_1_out_23), .out_24(cs2_1_out_24), .out_25(cs2_1_out_25), .out_27(cs2_1_out_27),
    .out_28(cs2_1_out_28), .out_29(cs2_1_out_29), .out_30(cs2_1_out_30), .AO(rom_2_data[8]),
    .OCP(rom_2_data[7]), .in_17(rom_2_data[6]), .\自动_手动 (\自动_手动 ), .SEG_2(rom_2_data[0]),
    .KEY_2(rom_2_data[1]), .KEY_4(rom_2_data[2]), .R0_2(rom_2_data[3]), .Rd_2(rom_2_data[4]),
    .R1_2(rom_2_data[5]));  // open: out_26, OCP_2, in_19, AO_2, in_21
  addr8 addr8_1 (
    .A2(reg8_1_out_10), .A1(reg8_1_out_11), .A2_2(reg8_1_out_12), .A1_2(reg8_1_out_13), .A0(reg8_1_out_14),
    .A2_3(reg8_1_out_15), .A1_3(reg8_1_out_16), .A0_2(reg8_1_out_17), .B2(reg8_2_out_10), .B1(reg8_2_out_11),
    .B2_2(reg8_2_out_12), .B1_2(reg8_2_out_13), .B0(reg8_2_out_14), .B2_3(reg8_2_out_15),
    .B1_3(reg8_2_out_16), .B0_2(reg8_2_out_17), .rd(cs2_1_out_29), .S2(Ain_out_10[0]), .S1(Ain_out_10[1]),
    .S2_2(Ain_out_10[2]), .S1_2(Ain_out_10[3]), .S0(Ain_out_10[4]), .S2_3(Ain_out_10[5]), .S1_3(Ain_out_16),
    .S0_2(Ain_out_17));
  _7_Segment_Display #(.active("false")) u_7_segment_display_1 (
    .g(seg2_1_out_23), .f(seg2_1_out_22), .a(seg2_1_out_17), .b(seg2_1_out_18), .e(seg2_1_out_21),
    .d(seg2_1_out_20), .c(seg2_1_out_19), .dp(1'b1));
  reg8 reg8_2 (
    .out_10(reg8_2_out_10), .out_11(reg8_2_out_11), .out_12(reg8_2_out_12), .out_13(reg8_2_out_13),
    .out_14(reg8_2_out_14), .out_15(reg8_2_out_15), .out_16(reg8_2_out_16), .out_17(reg8_2_out_17),
    .in_2(reg8_1_out_10), .in_3(reg8_1_out_11), .in_4(reg8_1_out_12), .in_5(reg8_1_out_13),
    .in_6(reg8_1_out_14), .in_7(reg8_1_out_15), .in_8(reg8_1_out_16), .in_9(reg8_1_out_17),
    .in_1(cs2_1_out_27));
  _7_Segment_Display #(.active("false")) u_7_segment_display_2 (
    .g(seg2_1_out_16), .f(seg2_1_out_15), .a(seg2_1_out_10), .b(seg2_1_out_11), .e(seg2_1_out_14),
    .d(seg2_1_out_13), .c(seg2_1_out_12), .dp(1'b1));
  ROM #(.addrWidth(10), .dataWidth(9)) rom_2 (.addr(counter_1_q_2), .data(rom_2_data));  // open: sel
  reg8 reg8_3 (
    .out_10(counter_1_q_2[9]), .out_11(counter_1_q_2[8]), .out_12(counter_1_q_2[7]),
    .out_13(counter_1_q_2[6]), .out_14(counter_1_q_2[5]), .out_15(counter_1_q_2[4]),
    .out_16(counter_1_q_2[3]), .out_17(counter_1_q_2[2]), .in_2(Ain_out_17), .in_3(Ain_out_16),
    .in_4(Ain_out_10[5]), .in_5(Ain_out_10[4]), .in_6(Ain_out_10[3]), .in_7(Ain_out_10[2]),
    .in_8(Ain_out_10[1]), .in_9(Ain_out_10[0]), .in_1(counter_1_q_2[0]));
  Counter #(.width(6), .max('h3f)) counter_1 (
    .D(Ain_out_10), .Q({counter_1_q, counter_1_q_2[1:0]}), .clk(clock_1_out));  // open: load, count, carry, clr
  Clock clock_1 (.out(clock_1_out));

  // Notes on the sheet:
  //   contents of rom_1 (hex, n*v repeats v):
  //   14
  //   “外码"
endmodule

module _8_3 (
  input  i0,
  input  i1,
  input  i2,
  input  i3,
  input  i4,
  input  i5,
  input  i6,
  input  i7,
  output y0,
  output y1,
  output y2
);

  or or_1 (y0, i1, i3, i5, i7);
  or or_2 (y1, i2, i3, i6, i7);
  or or_3 (y2, i4, i5, i6, i7);
endmodule

module _138 (
  input  in_1,
  input  in_2,
  input  in_3,
  output out_4,
  output out_5,
  output out_6,
  output out_7,
  output out_8,
  output out_9,
  output out_10,
  output out_11
);

  wire not_1_out, not_2_out, not_3_out;

  not not_1 (not_1_out, in_1);
  not not_2 (not_2_out, in_2);
  not not_3 (not_3_out, in_3);
  and and_1 (out_4, not_1_out, not_2_out, not_3_out);
  and and_2 (out_5, in_1, not_2_out, not_3_out);
  and and_3 (out_6, not_1_out, in_2, not_3_out);
  and and_4 (out_7, in_1, in_2, not_3_out);
  and and_5 (out_8, not_1_out, not_2_out, in_3);
  and and_6 (out_9, in_1, not_2_out, in_3);
  and and_7 (out_10, not_1_out, in_2, in_3);
  and and_8 (out_11, in_1, in_2, in_3);
endmodule

// CN1
module counter1 (
  input  T_CE,
  output out_2
);

  wire clock_1_out;

  Clock clock_1 (.out(clock_1_out));
  T_Flip_Flop t_ff_1 (.clk(clock_1_out), .T(T_CE), .Q(out_2));  // open: Qn, preset, reset, en

  // Notes on the sheet:
  //   CP
endmodule

module counter4 (
  input  T_CE,
  output out_2,
  output out_3,
  output out_4,
  output out_5
);

  wire clock_1_out, not_1_out, not_2_out, not_3_out;

  Clock clock_1 (.out(clock_1_out));
  not not_1 (not_1_out, out_3);
  not not_2 (not_2_out, out_4);
  not not_3 (not_3_out, out_5);
  T_Flip_Flop t_ff_1 (.clk(not_1_out), .T(T_CE), .Q(out_2));  // open: Qn, preset, reset, en
  T_Flip_Flop t_ff_2 (.clk(not_2_out), .T(T_CE), .Q(out_3));  // open: Qn, preset, reset, en
  T_Flip_Flop t_ff_3 (.clk(not_3_out), .T(T_CE), .Q(out_4));  // open: Qn, preset, reset, en
  T_Flip_Flop t_ff_4 (.clk(clock_1_out), .T(T_CE), .Q(out_5));  // open: Qn, preset, reset, en
  Counter counter_1 ();  // open: load, D, count, Q, carry, clk, clr

  // Notes on the sheet:
  //   CP
endmodule

// CN
module counter3 (
  input  T_CE,
  output out_2,
  output out_3,
  output out_4
);

  wire clock_1_out, not_1_out, not_2_out;

  Clock clock_1 (.out(clock_1_out));
  not not_1 (not_1_out, out_2);
  not not_2 (not_2_out, out_3);
  T_Flip_Flop t_ff_1 (.clk(clock_1_out), .T(T_CE), .Q(out_2));  // open: Qn, preset, reset, en
  T_Flip_Flop t_ff_2 (.clk(not_1_out), .T(T_CE), .Q(out_3));  // open: Qn, preset, reset, en
  T_Flip_Flop t_ff_3 (.clk(not_2_out), .T(T_CE), .Q(out_4));  // open: Qn, preset, reset, en

  // Notes on the sheet:
  //   CP
endmodule

// ctr
module ctrA (
  input  _0,
  input  _1,
  input  _2,
  input  _3,
  input  _4,
  input  _5,
  input  _6,
  input  _7,
  output SEG,
  output KEY,
  output KEY_2,
  output R0,
  output Rd,
  output R1,
  output out_15,
  output OCP,
  output A1
);

  or or_1 (KEY, _0, _1);
  or or_2 (KEY_2, _4, _5);
  or or_3 (R0, _0, _4, _6);
  or or_4 (Rd, _2, _3, _7);
  or or_5 (A1, _6, _7);

  assign OCP = _5;
  assign out_15 = 1'b0;
  assign R1 = _2;
  assign SEG = 1'b1;
endmodule

module ctrlzzs (
  input  in_1,
  input  in_2,
  input  in_3,
  input  in_4,
  input  in_5,
  input  in_6,
  output SEG,
  output KEY0,
  output KEY1,
  output R0,
  output R1
);

  or or_1 (KEY0, in_1, in_2, in_3);
  or or_2 (KEY1, in_4, in_6, in_5);

  assign R0 = in_3;
  assign R1 = in_5;
  assign SEG = 1'b1;
endmodule

// Driver
module ctrPower (
  input  SEG,
  input  KEY,
  input  KEY_2,
  input  R0,
  input  Rd,
  input  R1,
  input  in_7,
  input  OCP,
  input  A1,
  output out_10,
  output out_11,
  output out_12,
  output out_13,
  output out_14,
  output out_15,
  output out_16,
  output out_17,
  output out_18
);

  wire not_1_out, not_2_out, not_3_out, not_4_out, not_5_out, not_6_out, not_7_out, not_8_out, not_9_out,
       not_15_out, not_16_out, not_18_out, not_19_out, not_20_out, not_21_out;

  not not_1 (not_1_out, SEG);
  not not_2 (not_2_out, KEY);
  not not_3 (not_3_out, KEY_2);
  not not_4 (not_4_out, R0);
  not not_5 (not_5_out, Rd);
  not not_6 (not_6_out, R1);
  not not_7 (not_7_out, in_7);
  not not_8 (not_8_out, OCP);
  not not_9 (not_9_out, A1);
  not not_10 (out_18, not_1_out);
  not not_11 (out_17, not_2_out);
  not not_12 (out_16, not_3_out);
  not not_13 (out_15, not_4_out);
  not not_14 (out_14, not_5_out);
  not not_15 (not_15_out, not_6_out);
  not not_16 (not_16_out, not_15_out);
  not not_17 (out_12, not_7_out);
  not not_18 (not_18_out, not_8_out);
  not not_19 (not_19_out, not_18_out);
  not not_20 (not_20_out, not_9_out);
  not not_21 (not_21_out, not_20_out);
  not not_22 (out_13, not_16_out);
  not not_23 (out_11, not_19_out);
  not not_24 (out_10, not_21_out);
endmodule

module Cselect (
  input  in_1,
  input  in_2,
  input  in_3,
  input  in_4,
  input  in_5,
  input  in_6,
  input  in_7,
  input  in_8,
  input  in_9,
  input  in_10,
  input  in_11,
  input  in_12,
  input  in_13,
  input  in_14,
  input  in_15,
  input  in_16,
  input  in_17,
  output out_18,
  output out_19,
  output out_20,
  output out_21,
  output out_22,
  output out_23,
  output out_24,
  output out_25,
  output out_26,
  output out_27,
  output out_28,
  output out_29,
  output out_30,
  output out_31,
  output out_32,
  output out_33
);

  wire not_1_out;

  assign out_18 = not_1_out ? in_1 : 1'bz;  // Controlled_Buffer controlled_buffer_1
  assign out_19 = not_1_out ? in_2 : 1'bz;  // Controlled_Buffer controlled_buffer_2
  assign out_20 = not_1_out ? in_3 : 1'bz;  // Controlled_Buffer controlled_buffer_3
  assign out_21 = not_1_out ? in_4 : 1'bz;  // Controlled_Buffer controlled_buffer_4
  assign out_22 = not_1_out ? in_5 : 1'bz;  // Controlled_Buffer controlled_buffer_5
  assign out_23 = not_1_out ? in_6 : 1'bz;  // Controlled_Buffer controlled_buffer_6
  assign out_24 = not_1_out ? in_7 : 1'bz;  // Controlled_Buffer controlled_buffer_7
  assign out_25 = not_1_out ? in_8 : 1'bz;  // Controlled_Buffer controlled_buffer_8
  assign out_20 = in_17 ? in_11 : 1'bz;  // Controlled_Buffer controlled_buffer_9
  assign out_19 = in_17 ? in_10 : 1'bz;  // Controlled_Buffer controlled_buffer_10
  assign out_18 = in_17 ? in_9 : 1'bz;  // Controlled_Buffer controlled_buffer_11
  assign out_22 = in_17 ? in_13 : 1'bz;  // Controlled_Buffer controlled_buffer_12
  assign out_21 = in_17 ? in_12 : 1'bz;  // Controlled_Buffer controlled_buffer_13
  assign out_24 = in_17 ? in_15 : 1'bz;  // Controlled_Buffer controlled_buffer_14
  assign out_23 = in_17 ? in_14 : 1'bz;  // Controlled_Buffer controlled_buffer_15
  assign out_25 = in_17 ? in_16 : 1'bz;  // Controlled_Buffer controlled_buffer_16
  not not_1 (not_1_out, in_17);

  assign out_26 = out_18;
  assign out_27 = out_22;
  assign out_28 = out_19;
  assign out_29 = out_23;
  assign out_30 = out_20;
  assign out_31 = out_24;
  assign out_32 = out_21;
  assign out_33 = out_25;
endmodule

module CS (
  input  in_1,
  input  in_2,
  input  in_3,
  input  in_4,
  input  in_5,
  input  in_6,
  input  in_7,
  input  in_8,
  input  in_9,
  input  in_10,
  input  in_11,
  input  in_12,
  input  in_13,
  input  in_14,
  input  in_15,
  input  in_16,
  input  in_17,
  output out_18,
  output out_19,
  output out_20,
  output out_21,
  output out_22,
  output out_23,
  output out_24,
  output out_25
);

  wire not_1_out;

  assign out_18 = not_1_out ? in_1 : 1'bz;  // Controlled_Buffer controlled_buffer_1
  assign out_19 = not_1_out ? in_2 : 1'bz;  // Controlled_Buffer controlled_buffer_2
  assign out_21 = not_1_out ? in_4 : 1'bz;  // Controlled_Buffer controlled_buffer_3
  assign out_20 = not_1_out ? in_3 : 1'bz;  // Controlled_Buffer controlled_buffer_4
  assign out_23 = not_1_out ? in_6 : 1'bz;  // Controlled_Buffer controlled_buffer_5
  assign out_22 = not_1_out ? in_5 : 1'bz;  // Controlled_Buffer controlled_buffer_6
  assign out_24 = not_1_out ? in_7 : 1'bz;  // Controlled_Buffer controlled_buffer_7
  assign out_25 = not_1_out ? in_8 : 1'bz;  // Controlled_Buffer controlled_buffer_8
  assign out_20 = in_17 ? in_11 : 1'bz;  // Controlled_Buffer controlled_buffer_9
  assign out_19 = in_17 ? in_10 : 1'bz;  // Controlled_Buffer controlled_buffer_10
  assign out_18 = in_17 ? in_9 : 1'bz;  // Controlled_Buffer controlled_buffer_11
  assign out_21 = in_17 ? in_12 : 1'bz;  // Controlled_Buffer controlled_buffer_12
  assign out_22 = in_17 ? in_13 : 1'bz;  // Controlled_Buffer controlled_buffer_13
  assign out_25 = in_17 ? in_16 : 1'bz;  // Controlled_Buffer controlled_buffer_14
  assign out_24 = in_17 ? in_15 : 1'bz;  // Controlled_Buffer controlled_buffer_15
  assign out_23 = in_17 ? in_14 : 1'bz;  // Controlled_Buffer controlled_buffer_16
  not not_1 (not_1_out, in_17);
endmodule

module CS1 (
  input  in_1,
  input  in_2,
  input  in_3,
  input  in_4,
  input  in_5,
  input  in_6,
  input  in_7,
  input  in_8,
  input  in_9,
  input  in_10,
  input  in_11,
  input  in_12,
  input  in_13,
  input  in_14,
  input  in_15,
  input  in_16,
  input  in_17,
  output out_18,
  output out_19,
  output out_20,
  output out_21,
  output out_22,
  output out_23,
  output out_24,
  output out_25
);

  assign out_18 = out_25 ? in_1 : 1'bz;  // Controlled_Buffer controlled_buffer_1
  assign out_19 = out_25 ? in_3 : 1'bz;  // Controlled_Buffer controlled_buffer_2
  assign out_20 = out_25 ? in_5 : 1'bz;  // Controlled_Buffer controlled_buffer_3
  assign out_21 = out_25 ? in_7 : 1'bz;  // Controlled_Buffer controlled_buffer_4
  assign out_22 = out_25 ? in_9 : 1'bz;  // Controlled_Buffer controlled_buffer_5
  assign out_23 = out_25 ? in_11 : 1'bz;  // Controlled_Buffer controlled_buffer_6
  assign out_24 = out_25 ? in_13 : 1'bz;  // Controlled_Buffer controlled_buffer_7
  Controlled_Buffer controlled_buffer_8 (.in(in_15), .en(out_25));  // open: out
  not not_1 (out_25, in_17);
  assign out_18 = in_17 ? in_2 : 1'bz;  // Controlled_Buffer controlled_buffer_9
  assign out_19 = in_17 ? in_4 : 1'bz;  // Controlled_Buffer controlled_buffer_10
  assign out_20 = in_17 ? in_6 : 1'bz;  // Controlled_Buffer controlled_buffer_11
  assign out_21 = in_17 ? in_8 : 1'bz;  // Controlled_Buffer controlled_buffer_12
  assign out_22 = in_17 ? in_10 : 1'bz;  // Controlled_Buffer controlled_buffer_13
  assign out_23 = in_17 ? in_12 : 1'bz;  // Controlled_Buffer controlled_buffer_14
  assign out_24 = in_17 ? in_14 : 1'bz;  // Controlled_Buffer controlled_buffer_15
  assign out_25 = in_17 ? in_16 : 1'bz;  // Controlled_Buffer controlled_buffer_16
endmodule

module CS2 (
  input  \自动_手动 ,
  input  SEG,
  input  SEG_2,
  input  KEY,
  input  KEY_2,
  input  KEY_3,
  input  KEY_4,
  input  R0,
  input  R0_2,
  input  Rd,
  input  Rd_2,
  input  R1,
  input  R1_2,
  input  in_14,
  input  AO,
  input  OCP,
  input  in_17,
  input  OCP_2,
  input  in_19,
  input  AO_2,
  input  in_21,
  output out_22,
  output out_23,
  output out_24,
  output out_25,
  output out_26,
  output out_27,
  output out_28,
  output out_29,
  output out_30
);

  wire not_1_out;

  assign out_22 = not_1_out ? SEG : 1'bz;  // Controlled_Buffer controlled_buffer_1
  assign out_23 = not_1_out ? KEY : 1'bz;  // Controlled_Buffer controlled_buffer_2
  assign out_24 = not_1_out ? KEY_3 : 1'bz;  // Controlled_Buffer controlled_buffer_3
  assign out_25 = not_1_out ? R0 : 1'bz;  // Controlled_Buffer controlled_buffer_4
  assign out_26 = not_1_out ? Rd : 1'bz;  // Controlled_Buffer controlled_buffer_5
  assign out_27 = not_1_out ? R1 : 1'bz;  // Controlled_Buffer controlled_buffer_6
  assign out_28 = not_1_out ? in_14 : 1'bz;  // Controlled_Buffer controlled_buffer_7
  assign out_29 = not_1_out ? OCP_2 : 1'bz;  // Controlled_Buffer controlled_buffer_8
  assign out_30 = not_1_out ? AO_2 : 1'bz;  // Controlled_Buffer controlled_buffer_9
  not not_1 (not_1_out, \自动_手动 );
  assign out_22 = \自动_手动  ? SEG_2 : 1'bz;  // Controlled_Buffer controlled_buffer_10
  assign out_23 = \自动_手动  ? KEY_2 : 1'bz;  // Controlled_Buffer controlled_buffer_11
  assign out_24 = \自动_手动  ? KEY_4 : 1'bz;  // Controlled_Buffer controlled_buffer_12
  assign out_25 = \自动_手动  ? R0_2 : 1'bz;  // Controlled_Buffer controlled_buffer_13
  assign out_26 = \自动_手动  ? Rd_2 : 1'bz;  // Controlled_Buffer controlled_buffer_14
  assign out_27 = \自动_手动  ? R1_2 : 1'bz;  // Controlled_Buffer controlled_buffer_15
  assign out_30 = \自动_手动  ? AO : 1'bz;  // Controlled_Buffer controlled_buffer_16
  assign out_28 = \自动_手动  ? in_17 : 1'bz;  // Controlled_Buffer controlled_buffer_17
  assign out_29 = \自动_手动  ? OCP : 1'bz;  // Controlled_Buffer controlled_buffer_18

  // Notes on the sheet:
  //   手动
  //   手动
  //   -+
  //   自动
endmodule

module C24 (
  input  in_1,
  input  in_2,
  input  in_3,
  input  in_4,
  input  in_5,
  output out_6,
  output out_7,
  output out_8,
  output out_9,
  output out_10,
  output out_11,
  output out_12,
  output out_13
);

  wire not_1_out;

  not not_1 (not_1_out, in_1);
  assign out_6 = in_1 ? in_2 : 1'bz;  // Controlled_Buffer controlled_buffer_1
  assign out_7 = in_1 ? in_3 : 1'bz;  // Controlled_Buffer controlled_buffer_2
  assign out_8 = in_1 ? in_4 : 1'bz;  // Controlled_Buffer controlled_buffer_3
  assign out_9 = in_1 ? in_5 : 1'bz;  // Controlled_Buffer controlled_buffer_4
  assign out_10 = not_1_out ? in_2 : 1'bz;  // Controlled_Buffer controlled_buffer_5
  assign out_11 = not_1_out ? in_3 : 1'bz;  // Controlled_Buffer controlled_buffer_6
  assign out_12 = not_1_out ? in_4 : 1'bz;  // Controlled_Buffer controlled_buffer_7
  assign out_13 = not_1_out ? in_5 : 1'bz;  // Controlled_Buffer controlled_buffer_8
endmodule

module ctrS (
  input  _0,
  input  _1,
  input  _2,
  input  _3,
  input  _4,
  input  _5,
  input  _6,
  input  _7,
  output SEG,
  output KEY,
  output KEY_2,
  output R0,
  output Rd,
  output R1,
  output out_15,
  output OCP,
  output A1
);

  or or_1 (KEY, _0, _1);
  or or_2 (KEY_2, _4, _5);
  or or_3 (R0, _0, _4, _6);
  or or_4 (Rd, _2, _3, _7);
  or or_5 (A1, _6, _7);

  assign OCP = _5;
  assign out_15 = 1'b1;
  assign R1 = _2;
  assign SEG = 1'b1;
endmodule

// C24
module C224 (
  input  in_1,
  input  in_2,
  input  in_3,
  input  in_4,
  input  in_5,
  output out_6,
  output out_7,
  output out_8,
  output out_9,
  output out_10,
  output out_11,
  output out_12,
  output out_13
);

  wire not_1_out;

  assign out_7 = in_5 ? in_1 : 1'bz;  // Controlled_Buffer controlled_buffer_1
  assign out_8 = in_5 ? in_2 : 1'bz;  // Controlled_Buffer controlled_buffer_2
  assign out_9 = in_5 ? in_3 : 1'bz;  // Controlled_Buffer controlled_buffer_3
  assign out_6 = in_5 ? in_4 : 1'bz;  // Controlled_Buffer controlled_buffer_4
  not not_1 (not_1_out, in_5);
  assign out_10 = not_1_out ? in_1 : 1'bz;  // Controlled_Buffer controlled_buffer_5
  assign out_11 = not_1_out ? in_2 : 1'bz;  // Controlled_Buffer controlled_buffer_6
  assign out_12 = not_1_out ? in_3 : 1'bz;  // Controlled_Buffer controlled_buffer_7
  assign out_13 = not_1_out ? in_4 : 1'bz;  // Controlled_Buffer controlled_buffer_8
endmodule

module keyboard (
  input  \输入0 ,
  input  in_2,
  input  _1,
  input  _2,
  input  _3,
  input  _4,
  input  _5,
  input  _6,
  input  _7,
  output out_10,
  output out_11,
  output out_12,
  output out_13
);

  wire n8_3_1_y0, n8_3_1_y1, n8_3_1_y2, undriven;

  _8_3 u_8_3_1 (
    .i0(\输入0 ), .i1(_1), .i2(_2), .i3(_3), .i4(_4), .i5(undriven), .i6(_6), .i7(_7), .y0(n8_3_1_y0),
    .y1(n8_3_1_y1), .y2(n8_3_1_y2));
  c4 c4_1 (
    .in_2(n8_3_1_y0), .in_3(n8_3_1_y1), .in_4(n8_3_1_y2), .in_5(1'b0), .in_1(in_2), .out_6(out_10),
    .out_7(out_11), .out_8(out_12), .out_9(out_13));

  // Notes on the sheet:
  //   “外码"
  //   0
endmodule

module _16_4 (
  input  i0,
  input  i1,
  input  i2,
  input  i3,
  input  i4,
  input  i5,
  input  i6,
  input  i7,
  input  i0_2,
  input  i1_2,
  input  i2_2,
  input  i3_2,
  input  i4_2,
  input  i5_2,
  input  i6_2,
  input  i7_2,
  output y0,
  output y1,
  output y2,
  output out_20
);

  or or_1 (y0, i1, i3, i5, i7, i1_2, i3_2, i5_2, i7_2);
  or or_2 (y1, i2, i3, i6, i7, i2_2, i3_2, i6_2, i7_2);
  or or_3 (y2, i4, i5, i6, i7, i4_2, i5_2, i6_2, i7_2);
  or or_4 (out_20, i0_2, i1_2, i2_2, i3_2, i4_2, i5_2, i6_2, i7_2);

  // Notes on the sheet:
  //   y3
endmodule

module key_16 (
  input  i0,
  input  i1,
  input  i2,
  input  i3,
  input  i4,
  input  i5,
  input  i6,
  input  i7,
  input  i0_2,
  input  i1_2,
  input  i2_2,
  input  i3_2,
  input  in_13,
  input  i4_2,
  input  i5_2,
  input  i6_2,
  input  i7_2,
  input  i0_3,
  input  i1_3,
  input  i2_3,
  input  i3_3,
  input  i4_3,
  input  i5_3,
  input  i6_3,
  input  i7_3,
  input  i0_4,
  input  i1_4,
  input  i2_4,
  input  i3_4,
  input  i4_4,
  input  i5_4,
  input  i6_4,
  input  i7_4,
  output y0,
  output y1,
  output y2,
  output y3,
  output y0_2,
  output y1_2,
  output y2_2,
  output y3_2
);

  wire n16_4_1_out_20, n16_4_1_y0, n16_4_1_y1, n16_4_1_y2, n16_4_2_out_20, n16_4_2_y0, n16_4_2_y1, n16_4_2_y2;

  _16_4 u_16_4_1 (
    .i0(i0), .i1(i1), .i2(i2), .i3(i3), .i4(i4), .i5(i5), .i6(i6), .i7(i7), .i0_2(i0_2), .i1_2(i1_2),
    .i2_2(i2_2), .i3_2(i3_2), .i4_2(i4_2), .i5_2(i5_2), .i6_2(i6_2), .i7_2(i7_2), .y0(n16_4_1_y0),
    .y1(n16_4_1_y1), .y2(n16_4_1_y2), .out_20(n16_4_1_out_20));
  _16_4 u_16_4_2 (
    .i0(i0_3), .i1(i1_3), .i2(i2_3), .i3(i3_3), .i4(i4_3), .i5(i5_3), .i6(i6_3), .i7(i7_3), .i0_2(i0_4),
    .i1_2(i1_4), .i2_2(i2_4), .i3_2(i3_4), .i4_2(i4_4), .i5_2(i5_4), .i6_2(i6_4), .i7_2(i7_4),
    .y0(n16_4_2_y0), .y1(n16_4_2_y1), .y2(n16_4_2_y2), .out_20(n16_4_2_out_20));
  c8 c8_1 (
    .in_1(in_13), .out_10(y0), .out_11(y1), .out_12(y2), .out_13(y3), .out_14(y0_2), .out_15(y1_2),
    .out_16(y2_2), .out_17(y3_2), .in_2(n16_4_2_y0), .in_3(n16_4_2_y1), .in_4(n16_4_2_y2),
    .in_5(n16_4_2_out_20), .in_6(n16_4_1_y0), .in_7(n16_4_1_y1), .in_8(n16_4_1_y2), .in_9(n16_4_1_out_20));
endmodule

module seg2 (
  input  in_1,
  input  i0,
  input  i1,
  input  i2,
  input  i3,
  input  i4,
  input  i5,
  input  i6,
  input  i7,
  output out_10,
  output out_11,
  output out_12,
  output out_13,
  output out_14,
  output out_15,
  output out_16,
  output out_17,
  output out_18,
  output out_19,
  output out_20,
  output out_21,
  output out_22,
  output out_23
);

  wire c4_1_out_6, c4_1_out_7, c4_1_out_8, c4_1_out_9, c4_2_out_6, c4_2_out_7, c4_2_out_8, c4_2_out_9;

  c4 c4_1 (
    .in_2(i0), .in_3(i1), .in_4(i2), .in_5(i3), .in_1(in_1), .out_6(c4_1_out_6), .out_7(c4_1_out_7),
    .out_8(c4_1_out_8), .out_9(c4_1_out_9));
  c4 c4_2 (
    .in_2(i4), .in_3(i5), .in_4(i6), .in_5(i7), .in_1(in_1), .out_6(c4_2_out_6), .out_7(c4_2_out_7),
    .out_8(c4_2_out_8), .out_9(c4_2_out_9));
  Digital digital_1 (
    .D0(c4_1_out_6), .D1(c4_1_out_7), .D2(c4_1_out_8), .D3(c4_1_out_9), .a(out_10), .b(out_11), .c(out_12),
    .d(out_13), .e(out_14), .f(out_15), .g(out_16));
  Digital digital_2 (
    .D0(c4_2_out_6), .D1(c4_2_out_7), .D2(c4_2_out_8), .D3(c4_2_out_9), .a(out_17), .b(out_18), .c(out_19),
    .d(out_20), .e(out_21), .f(out_22), .g(out_23));
endmodule

module reg8 (
  input  in_1,
  input  in_2,
  input  in_3,
  input  in_4,
  input  in_5,
  input  in_6,
  input  in_7,
  input  in_8,
  input  in_9,
  output out_10,
  output out_11,
  output out_12,
  output out_13,
  output out_14,
  output out_15,
  output out_16,
  output out_17
);

  MS ms_1 (.out_4(out_10), .in_1(in_2), .in_2(in_1));  // open: out_3
  MS ms_2 (.out_4(out_11), .in_1(in_3), .in_2(in_1));  // open: out_3
  MS ms_3 (.out_4(out_12), .in_1(in_4), .in_2(in_1));  // open: out_3
  MS ms_4 (.out_4(out_14), .in_1(in_6), .in_2(in_1));  // open: out_3
  MS ms_5 (.out_4(out_13), .in_1(in_5), .in_2(in_1));  // open: out_3
  MS ms_6 (.out_4(out_15), .in_1(in_7), .in_2(in_1));  // open: out_3
  MS ms_7 (.out_4(out_16), .in_1(in_8), .in_2(in_1));  // open: out_3
  MS ms_8 (.out_4(out_17), .in_1(in_9), .in_2(in_1));  // open: out_3
endmodule

module cpu8 (
  input  in_1,
  input  in_2,
  input  in_3,
  input  in_4,
  input  in_5,
  input  in_6,
  input  in_7,
  input  in_8,
  input  in_9,
  input  in_10,
  input  in_11,
  input  in_12,
  input  in_13,
  input  in_14,
  input  in_15,
  input  in_16
);

  wire addr8_1_p4, addr8_1_p6, addr8_1_p11, addr8_1_p12, addr8_1_p13, addr8_1_p14, addr8_1_p15, addr8_1_p16,
       addr8_1_p17, addr8_1_p18, reg8_1_out_10, reg8_1_out_11, reg8_1_out_12, reg8_1_out_13, reg8_1_out_14,
       reg8_1_out_15, reg8_1_out_16, reg8_1_out_17;

  reg8 reg8_1 (
    .out_10(reg8_1_out_10), .out_11(reg8_1_out_11), .out_12(reg8_1_out_12), .out_13(reg8_1_out_13),
    .out_14(reg8_1_out_14), .out_15(reg8_1_out_15), .out_16(reg8_1_out_16), .out_17(reg8_1_out_17),
    .in_2(in_1), .in_3(in_2), .in_4(in_3), .in_5(in_4), .in_6(in_5), .in_7(in_6), .in_8(in_7), .in_9(in_8));  // open: in_1
  // addr8 addr8_1: pin names not known; wires that end beside it: reg8_1_out_10, reg8_1_out_11, reg8_1_out_12, addr8_1_p4, reg8_1_out_13, addr8_1_p6, reg8_1_out_14, reg8_1_out_15, reg8_1_out_16, reg8_1_out_17, addr8_1_p11, addr8_1_p12, addr8_1_p13, addr8_1_p14, addr8_1_p15, addr8_1_p16, addr8_1_p17, addr8_1_p18
  reg8 reg8_2 (
    .out_10(addr8_1_p11), .out_11(addr8_1_p12), .out_12(addr8_1_p13), .out_13(addr8_1_p14),
    .out_14(addr8_1_p15), .out_15(addr8_1_p16), .out_16(addr8_1_p17), .out_17(addr8_1_p18), .in_2(in_9),
    .in_3(in_10), .in_4(in_11), .in_5(in_12), .in_6(in_13), .in_7(in_14), .in_8(in_15), .in_9(in_16));  // open: in_1
endmodule

module c8 (
  input  in_1,
  input  in_2,
  input  in_3,
  input  in_4,
  input  in_5,
  input  in_6,
  input  in_7,
  input  in_8,
  input  in_9,
  output out_10,
  output out_11,
  output out_12,
  output out_13,
  output out_14,
  output out_15,
  output out_16,
  output out_17
);

  assign out_10 = in_1 ? in_2 : 1'bz;  // Controlled_Buffer controlled_buffer_1
  assign out_11 = in_1 ? in_3 : 1'bz;  // Controlled_Buffer controlled_buffer_2
  assign out_12 = in_1 ? in_4 : 1'bz;  // Controlled_Buffer controlled_buffer_3
  assign out_13 = in_1 ? in_5 : 1'bz;  // Controlled_Buffer controlled_buffer_4
  assign out_15 = in_1 ? in_7 : 1'bz;  // Controlled_Buffer controlled_buffer_5
  assign out_14 = in_1 ? in_6 : 1'bz;  // Controlled_Buffer controlled_buffer_6
  assign out_16 = in_1 ? in_8 : 1'bz;  // Controlled_Buffer controlled_buffer_7
  assign out_17 = in_1 ? in_9 : 1'bz;  // Controlled_Buffer controlled_buffer_8
endmodule

module regc8 (
  input  in_1,
  input  in_2,
  input  in_3,
  input  in_4,
  input  in_5,
  input  in_6,
  input  in_7,
  input  in_8,
  input  in_9,
  input  in_10,
  output out_11,
  output out_12,
  output out_13,
  output out_14,
  output out_15,
  output out_16,
  output out_17,
  output out_18
);

  wire ms_1_out_4, ms_2_out_4, ms_3_out_4, ms_4_out_4, ms_5_out_4, ms_6_out_4, ms_7_out_4, ms_8_out_4;

  assign out_11 = in_1 ? ms_1_out_4 : 1'bz;  // Controlled_Buffer controlled_buffer_1
  MS ms_1 (.out_4(ms_1_out_4), .in_1(in_3), .in_2(in_2));  // open: out_3
  assign out_12 = in_1 ? ms_2_out_4 : 1'bz;  // Controlled_Buffer controlled_buffer_2
  assign out_13 = in_1 ? ms_3_out_4 : 1'bz;  // Controlled_Buffer controlled_buffer_3
  MS ms_2 (.out_4(ms_2_out_4), .in_1(in_4), .in_2(in_2));  // open: out_3
  MS ms_3 (.out_4(ms_3_out_4), .in_1(in_5), .in_2(in_2));  // open: out_3
  assign out_14 = in_1 ? ms_4_out_4 : 1'bz;  // Controlled_Buffer controlled_buffer_4
  assign out_15 = in_1 ? ms_5_out_4 : 1'bz;  // Controlled_Buffer controlled_buffer_5
  MS ms_4 (.out_4(ms_4_out_4), .in_1(in_6), .in_2(in_2));  // open: out_3
  MS ms_5 (.out_4(ms_5_out_4), .in_1(in_7), .in_2(in_2));  // open: out_3
  assign out_16 = in_1 ? ms_6_out_4 : 1'bz;  // Controlled_Buffer controlled_buffer_6
  MS ms_6 (.out_4(ms_6_out_4), .in_1(in_8), .in_2(in_2));  // open: out_3
  assign out_18 = in_1 ? ms_8_out_4 : 1'bz;  // Controlled_Buffer controlled_buffer_7
  assign out_17 = in_1 ? ms_7_out_4 : 1'bz;  // Controlled_Buffer controlled_buffer_8
  MS ms_7 (.out_4(ms_7_out_4), .in_1(in_9), .in_2(in_2));  // open: out_3
  MS ms_8 (.out_4(ms_8_out_4), .in_1(in_10), .in_2(in_2));  // open: out_3
endmodule

module addr8 (
  input  A2,
  input  A1,
  input  rd,
  input  A2_2,
  input  A1_2,
  input  A0,
  input  A2_3,
  input  A1_3,
  input  A0_2,
  input  B2,
  input  B1,
  input  B2_2,
  input  B1_2,
  input  B0,
  input  B2_3,
  input  B1_3,
  input  B0_2,
  output S2,
  output S1,
  output S2_2,
  output S1_2,
  output S0,
  output S2_3,
  output S1_3,
  output S0_2
);

  wire fa_1_co, fa_1_s, fa_2_co, fa_2_s, fa_3_co, fa_3_s, fa_4_co, fa_4_s, fa_5_co, fa_5_s, fa_6_co, fa_6_s,
       fa_7_co, fa_7_s, fa_8_co, fa_8_s;

  fa fa_1 (.Ci(A0_2), .B(B0_2), .A(1'b0), .S(fa_1_s), .Co(fa_1_co));
  fa fa_2 (.Ci(A1_3), .B(B1_3), .A(fa_1_co), .S(fa_2_s), .Co(fa_2_co));
  fa fa_3 (.Ci(A0), .B(B0), .A(fa_4_co), .S(fa_3_s), .Co(fa_3_co));
  fa fa_4 (.Ci(fa_2_co), .B(A2_3), .A(B2_3), .S(fa_4_s), .Co(fa_4_co));
  fa fa_5 (.Ci(A1_2), .B(B1_2), .A(fa_3_co), .S(fa_5_s), .Co(fa_5_co));
  fa fa_6 (.Ci(fa_5_co), .B(A2_2), .A(B2_2), .S(fa_6_s), .Co(fa_6_co));
  fa fa_7 (.Ci(A2), .B(B2), .A(fa_8_co), .S(fa_7_s), .Co(fa_7_co));
  fa fa_8 (.Ci(A1), .B(B1), .A(fa_6_co), .S(fa_8_s), .Co(fa_8_co));
  c8 c8_1 (
    .in_1(rd), .out_10(S2), .out_11(S1), .out_12(S2_2), .out_13(S1_2), .out_14(S0), .out_15(S2_3),
    .out_16(S1_3), .out_17(S0_2), .in_2(fa_7_s), .in_3(fa_8_s), .in_4(fa_6_s), .in_5(fa_5_s), .in_6(fa_3_s),
    .in_7(fa_4_s), .in_8(fa_2_s), .in_9(fa_1_s));

  // Notes on the sheet:
  //   Ci
  //   C
endmodule

module CPU8n (
  input  in_1,
  input  in_2,
  input  in_3,
  input  in_4,
  input  in_5,
  input  in_6,
  input  in_7,
  input  in_8,
  input  in_9,
  input  in_10,
  input  in_11,
  input  in_12
);

  wire addr8_1_p16, addr8_1_p18, addr8_1_p20, addr8_1_p21, addr8_1_p22, addr8_1_p23, addr8_1_p24,
       addr8_1_p25, addr8_1_p26, reg8_1_out_10, reg8_1_out_11, reg8_1_out_12, reg8_1_out_13, reg8_1_out_14,
       reg8_1_out_15, reg8_1_out_16, reg8_1_out_17;

  c8 c8_1 (
    .in_1(in_9), .out_10(in_8), .out_11(in_7), .out_12(in_6), .out_13(in_5), .out_14(in_4), .out_15(in_3),
    .out_16(in_2), .out_17(in_1), .in_2(reg8_1_out_17), .in_3(reg8_1_out_16), .in_4(reg8_1_out_15),
    .in_5(reg8_1_out_14), .in_6(reg8_1_out_13), .in_7(reg8_1_out_12), .in_8(reg8_1_out_11),
    .in_9(reg8_1_out_10));
  reg8 reg8_1 (
    .out_10(reg8_1_out_10), .out_11(reg8_1_out_11), .out_12(reg8_1_out_12), .out_13(reg8_1_out_13),
    .out_14(reg8_1_out_14), .out_15(reg8_1_out_15), .out_16(reg8_1_out_16), .out_17(reg8_1_out_17),
    .in_2(in_1), .in_3(in_2), .in_4(in_3), .in_5(in_4), .in_6(in_5), .in_7(in_6), .in_8(in_7), .in_9(in_8),
    .in_1(in_11));
  // addr8 addr8_1: pin names not known; wires that end beside it: in_10, reg8_1_out_10, reg8_1_out_11, reg8_1_out_12, in_1, reg8_1_out_13, in_2, reg8_1_out_14, in_3, reg8_1_out_15, in_4, reg8_1_out_16, in_5, reg8_1_out_17, in_6, addr8_1_p16, in_7, addr8_1_p18, in_8, addr8_1_p20, addr8_1_p21, addr8_1_p22, addr8_1_p23, addr8_1_p24, addr8_1_p25, addr8_1_p26
  reg8 reg8_2 (
    .out_10(addr8_1_p16), .out_11(addr8_1_p18), .out_12(addr8_1_p20), .out_13(addr8_1_p22),
    .out_14(addr8_1_p23), .out_15(addr8_1_p24), .out_16(addr8_1_p25), .out_17(addr8_1_p26),
    .in_2(reg8_1_out_10), .in_3(reg8_1_out_11), .in_4(reg8_1_out_12), .in_5(reg8_1_out_13),
    .in_6(reg8_1_out_14), .in_7(reg8_1_out_15), .in_8(reg8_1_out_16), .in_9(reg8_1_out_17), .in_1(in_12));
endmodule

module main3 (
  input  \输入0 ,
  input  _1,
  input  _2,
  input  _3,
  input  _4,
  input  _6,
  input  _7,
  input  \输入1 ,
  input  _1_2,
  input  \地址总线 ,
  input  _3_2,
  input  _4_2,
  input  _5,
  input  _6_2,
  input  in_15,
  input  _7_2,
  input  SEG,
  input  KEY,
  input  KEY_2,
  input  R0,
  input  Rd,
  input  R1,
  input  in_23,
  input  OCP,
  input  AO
);

  wire aif_1_c, aif_1_out_12, aif_1_s0, aif_1_s1, aif_1_s2, c4_1_out_6, c4_1_out_7, c4_1_out_8, c4_1_out_9,
       c4_3_out_6, c4_3_out_7, c4_3_out_8, c4_3_out_9, c224_1_out_10, c224_1_out_11, c224_1_out_12,
       cs2_1_out_22, cs2_1_out_23, cs2_1_out_24, cs2_1_out_25, cs2_1_out_26, cs2_1_out_27, cs2_1_out_28,
       cs2_1_out_29, cs2_1_out_30, digital_1_a, digital_1_b, digital_1_c, digital_1_d, digital_1_e,
       digital_1_f, digital_1_g, n8_3_1_y0, n8_3_1_y1, n8_3_1_y2, n8_3_2_y0, n8_3_2_y1, n8_3_2_y2,
       n138_1_out_4, n138_1_out_5, n138_1_out_6, n138_1_out_7, n138_1_out_8, n138_1_out_9, n138_1_out_10,
       n138_1_out_11, r33_1_out_5, r33_1_out_6, r33_1_out_7, r33_2_out_5, r33_2_out_6, r33_2_out_7, undriven;
  wire [2:0] counter3_1_out_2;
  wire [8:0] rom_1_data;

  _8_3 u_8_3_1 (
    .i0(\输入0 ), .i1(_1), .i2(_2), .i3(_3), .i4(_4), .i5(undriven), .i6(_6), .i7(_7), .y0(n8_3_1_y0),
    .y1(n8_3_1_y1), .y2(n8_3_1_y2));
  _8_3 u_8_3_2 (
    .i0(\输入1 ), .i1(_1_2), .i2(1'b1), .i3(_3_2), .i4(_4_2), .i5(_5), .i6(_6_2), .i7(_7_2), .y0(n8_3_2_y0),
    .y1(n8_3_2_y1), .y2(n8_3_2_y2));
  LED led_1 (.in(c4_1_out_9));
  LED led_2 (.in(c4_1_out_8));
  c4 c4_1 (
    .in_2(n8_3_1_y0), .in_3(n8_3_1_y1), .in_4(n8_3_1_y2), .in_5(1'b0), .in_1(cs2_1_out_23),
    .out_6(c4_1_out_6), .out_7(c4_1_out_7), .out_8(c4_1_out_8), .out_9(c4_1_out_9));
  c4 c4_2 (
    .in_2(n8_3_2_y0), .in_3(n8_3_2_y1), .in_4(n8_3_2_y2), .in_5(1'b0), .in_1(cs2_1_out_24),
    .out_6(c4_1_out_6), .out_7(c4_1_out_7), .out_8(c4_1_out_8), .out_9(c4_1_out_9));
  CS2 cs2_1 (
    .SEG(SEG), .KEY(KEY), .KEY_3(KEY_2), .R0(R0), .Rd(Rd), .R1(R1), .in_14(in_23), .out_22(cs2_1_out_22),
    .out_23(cs2_1_out_23), .out_24(cs2_1_out_24), .out_25(cs2_1_out_25), .out_26(cs2_1_out_26),
    .out_27(cs2_1_out_27), .out_28(cs2_1_out_28), .out_29(cs2_1_out_29), .out_30(cs2_1_out_30), .OCP_2(OCP),
    .AO_2(AO), .AO(rom_1_data[0]), .OCP(rom_1_data[1]), .in_17(rom_1_data[2]), .\自动_手动 (\地址总线 ),
    .SEG_2(rom_1_data[8]), .KEY_2(rom_1_data[7]), .KEY_4(rom_1_data[6]), .R0_2(rom_1_data[5]),
    .Rd_2(rom_1_data[4]), .R1_2(rom_1_data[3]));  // open: in_19, in_21
  LED led_3 (.in(c4_1_out_7));
  LED led_4 (.in(c4_1_out_6));
  R33 r33_1 (
    .out_5(r33_1_out_5), .out_6(r33_1_out_6), .out_7(r33_1_out_7), .in_2(c4_1_out_8), .in_3(c4_1_out_7),
    .in_4(c4_1_out_6), .in_1(cs2_1_out_25));
  R33 r33_2 (
    .out_5(r33_2_out_5), .out_6(r33_2_out_6), .out_7(r33_2_out_7), .in_2(c4_1_out_8), .in_3(c4_1_out_7),
    .in_4(c4_1_out_6), .in_1(cs2_1_out_27));
  LED led_5 (.in(rom_1_data[7]));
  LED led_6 (.in(rom_1_data[8]));
  Digital digital_1 (
    .D0(c4_3_out_6), .D1(c4_3_out_7), .D2(c4_3_out_8), .D3(c4_3_out_9), .a(digital_1_a), .b(digital_1_b),
    .c(digital_1_c), .d(digital_1_d), .e(digital_1_e), .f(digital_1_f), .g(digital_1_g));
  c4 c4_3 (
    .in_2(c4_1_out_9), .in_3(c4_1_out_8), .in_4(c4_1_out_7), .in_5(c4_1_out_6), .in_1(cs2_1_out_22),
    .out_6(c4_3_out_6), .out_7(c4_3_out_7), .out_8(c4_3_out_8), .out_9(c4_3_out_9));
  C224 c224_1 (
    .in_1(r33_1_out_5), .in_2(r33_1_out_6), .in_3(r33_1_out_7), .in_4(1'b0), .out_6(c4_1_out_9),
    .out_7(c4_1_out_8), .out_8(c4_1_out_7), .out_9(c4_1_out_6), .in_5(cs2_1_out_26), .out_10(c224_1_out_10),
    .out_11(c224_1_out_11), .out_12(c224_1_out_12));  // open: out_13
  LED led_7 (.in(rom_1_data[4]));
  LED led_8 (.in(rom_1_data[5]));
  LED led_9 (.in(rom_1_data[6]));
  LED led_10 (.in(rom_1_data[3]));
  _7_Segment_Display #(.active("false")) u_7_segment_display_1 (
    .g(digital_1_g), .f(digital_1_f), .a(digital_1_a), .b(digital_1_b), .e(digital_1_e), .d(digital_1_d),
    .c(digital_1_c), .dp(1'b1));
  AIF aif_1 (
    .A2(c224_1_out_10), .A1(c224_1_out_11), .A0(c224_1_out_12), .B2(r33_2_out_5), .B1(r33_2_out_6),
    .B0(r33_2_out_7), .out_12(aif_1_out_12), .in_7(cs2_1_out_28), .C(aif_1_c), .S2(aif_1_s2), .S1(aif_1_s1),
    .S0(aif_1_s0));
  LED led_11 (.in(aif_1_out_12));
  LED led_12 (.in(rom_1_data[2]));
  LED led_13 (.in(rom_1_data[0]));
  LED led_14 (.in(rom_1_data[1]));
  MS3C ms3c_1 (
    .in_1(cs2_1_out_30), .out_7(c4_1_out_9), .out_8(c4_1_out_8), .out_9(c4_1_out_7), .out_10(c4_1_out_6),
    .in_3(aif_1_c), .in_4(aif_1_s2), .in_5(aif_1_s1), .in_6(aif_1_s0), .in_2(cs2_1_out_29));
  counter3 counter3_1 (
    .T_CE(\地址总线 ), .out_2(counter3_1_out_2[0]), .out_3(counter3_1_out_2[1]), .out_4(counter3_1_out_2[2]));
  _138 u_138_1 (
    .in_1(counter3_1_out_2[0]), .in_2(counter3_1_out_2[1]), .in_3(counter3_1_out_2[2]), .out_4(n138_1_out_4),
    .out_5(n138_1_out_5), .out_6(n138_1_out_6), .out_7(n138_1_out_7), .out_8(n138_1_out_8),
    .out_9(n138_1_out_9), .out_10(n138_1_out_10), .out_11(n138_1_out_11));
  ROM #(.addrWidth(3), .dataWidth(9)) rom_1 (.addr(counter3_1_out_2), .data(rom_1_data), .sel(in_15));
  LED led_15 (.in(n138_1_out_4));
  LED led_16 (.in(n138_1_out_5));
  LED led_17 (.in(n138_1_out_6));
  LED led_18 (.in(n138_1_out_7));
  LED led_19 (.in(n138_1_out_8));
  LED led_20 (.in(n138_1_out_9));
  LED led_21 (.in(n138_1_out_10));
  LED led_22 (.in(n138_1_out_11));

  // Notes on the sheet:
  //   “外码"
  //   0
  //   0
  //   2
  //   手自切换
  //   “内码”
  //   数据总线
  //   累加器A
  //   寄存器B
  //   “外码"
  //   AO
  //   运算器
  //   -+
  //   OCP
  //   输出
  //   控制总线
  //   门电路造计算机
  //   加法程序5+2=7
  //   2018.4.7.19:57
  //   Shou
  //   带置位计数器
  //   自动/手动
  //   contents of rom_1 (hex, n*v repeats v):
  //   1a0 180 118 110 160 142 121 110
  //   Input I1
  //   Mov A,B
  //   Input I2
  //   Add B
  //   Output
endmodule
