// Logisim project 12register.circ as structural Verilog: 14 circuits, main circuit main
// R3
module main (
  input  in_1,
  input  in_2,
  input  in_3,
  input  register3,
  output out_5,
  output out_6,
  output out_7
);

  D d_1 (.out_3(out_5), .in_1(in_1), .in_2(register3));  // open: out_4
  D d_2 (.out_3(out_7), .in_1(in_3), .in_2(register3));  // open: out_4
  D d_3 (.out_3(out_6), .in_1(in_2), .in_2(register3));  // open: out_4
endmodule

// RS
module rs (
  input  nS,
  input  in_2,
  output Q,
  output nQ
);

  nand nand_1 (Q, nS, nQ);
  nand nand_2 (nQ, Q, in_2);

  // Notes on the sheet:
  //   ~R
endmodule

module syn (
  input  in_1,
  input  in_2,
  input  in_3,
  output out_4,
  output out_5
);

  wire nand_2_out, nand_4_out;

  nand nand_1 (out_4, nand_2_out, out_5);
  nand nand_2 (nand_2_out, in_1, in_2);
  nand nand_3 (out_5, out_4, nand_4_out);
  nand nand_4 (nand_4_out, in_2, in_3);

  // Notes on the sheet:
  //   S
  //   Q
  //   CP
  //   ~Q
  //   R
endmodule

// D1
module D (
  input  in_1,
  input  in_2,
  output out_3,
  output out_4
);

  wire nand_2_out, nand_4_out, not_1_out;

  nand nand_1 (out_3, nand_2_out, out_4);
  nand nand_2 (nand_2_out, in_1, in_2);
  not not_1 (not_1_out, in_1);
  nand nand_3 (out_4, out_3, nand_4_out);
  nand nand_4 (nand_4_out, in_2, not_1_out);

  // Notes on the sheet:
  //   D
  //   Q
  //   CP
  //   ~Q
endmodule

module MS (
  input  in_1,
  input  in_2,
  output out_3,
  output out_4
);

  wire d_2_out_3, not_1_out;

  D d_1 (.out_3(out_4), .out_4(out_3), .in_1(d_2_out_3), .in_2(not_1_out));
  not not_1 (not_1_out, in_2);
  D d_2 (.out_3(d_2_out_3), .in_1(in_1), .in_2(in_2));  // open: out_4
endmodule

module T (
  input  in_1,
  input  in_2,
  input  in_3,
  output out_4
);

  wire nand_1_out, nand_2_out, nand_3_out, nand_6_out, not_1_out, not_2_out, not_3_out;

  nand nand_1 (nand_1_out, nand_2_out, nand_3_out);
  nand nand_2 (nand_2_out, nand_6_out, in_2);
  not not_1 (not_1_out, in_2);
  nand nand_3 (nand_3_out, not_1_out, out_4);
  nand nand_4 (out_4, in_1, nand_6_out);
  nand nand_5 (in_1, nand_1_out, in_3);
  not not_2 (not_2_out, nand_1_out);
  nand nand_6 (nand_6_out, out_4, not_3_out);
  not not_3 (not_3_out, in_1);
  nand nand_7 (not_3_out, in_3, not_2_out);
endmodule

// R3
module Ms3 (
  input  in_1,
  input  in_2,
  input  in_3,
  input  in_4,
  output out_5,
  output out_6,
  output out_7
);

  MS ms_1 (.out_4(out_5), .in_1(in_1), .in_2(in_4));  // open: out_3
  MS ms_2 (.out_4(out_7), .in_1(in_3), .in_2(in_4));  // open: out_3
  MS ms_3 (.out_4(out_6), .in_1(in_2), .in_2(in_4));  // open: out_3
endmodule

// D31
module MS3C (
  input  in_1,
  input  in_2,
  input  in_3,
  input  in_4,
  input  in_5,
  input  in_6,
  output out_7,
  output out_8,
  output out_9,
  output out_10
);

  wire ms_1_out_4, ms_2_out_4, ms_3_out_4, ms_4_out_4;

  assign out_7 = in_1 ? ms_1_out_4 : 1'bz;  // Controlled_Buffer controlled_buffer_1
  MS ms_1 (.out_4(ms_1_out_4), .in_1(in_3), .in_2(in_2));  // open: out_3
  assign out_9 = in_1 ? ms_2_out_4 : 1'bz;  // Controlled_Buffer controlled_buffer_2
  assign out_8 = in_1 ? ms_3_out_4 : 1'bz;  // Controlled_Buffer controlled_buffer_3
  MS ms_2 (.out_4(ms_2_out_4), .in_1(in_5), .in_2(in_2));  // open: out_3
  MS ms_3 (.out_4(ms_3_out_4), .in_1(in_4), .in_2(in_2));  // open: out_3
  assign out_10 = in_1 ? ms_4_out_4 : 1'bz;  // Controlled_Buffer controlled_buffer_4
  MS ms_4 (.out_4(ms_4_out_4), .in_1(in_6), .in_2(in_2));  // open: out_3
endmodule

module R33 (
  input  in_1,
  input  in_2,
  input  in_3,
  input  in_4,
  output out_5,
  output out_6,
  output out_7
);

  D d_1 (.out_3(out_5), .in_1(in_2), .in_2(in_1));  // open: out_4
  D d_2 (.out_3(out_6), .in_1(in_3), .in_2(in_1));  // open: out_4
  D d_3 (.out_3(out_7), .in_1(in_4), .in_2(in_1));  // open: out_4
endmodule

module T1 (
  input  S,
  input  R,
  input  CP,
  output out_4
);

  wire and_1_out, nand_1_out, nand_2_out, nand_3_out, nand_4_out, nand_5_out, nand_6_out, nand_8_out,
       not_1_out, not_2_out, not_3_out, not_4_out, or_1_out;

  not not_1 (not_1_out, and_1_out);
  not not_2 (not_2_out, CP);
  or or_1 (or_1_out, nand_8_out, S);
  and and_1 (and_1_out, or_1_out, R);
  nand nand_1 (nand_1_out, and_1_out, not_2_out);
  nand nand_2 (nand_2_out, not_1_out, not_2_out);
  nand nand_3 (nand_3_out, nand_1_out, nand_4_out);
  nand nand_4 (nand_4_out, nand_3_out, nand_2_out);
  not not_3 (not_3_out, not_2_out);
  not not_4 (not_4_out, nand_3_out);
  nand nand_5 (nand_5_out, nand_3_out, not_3_out);
  nand nand_6 (nand_6_out, not_4_out, not_3_out);
  nand nand_7 (out_4, nand_5_out, nand_8_out);
  nand nand_8 (nand_8_out, out_4, nand_6_out);
endmodule

module newRS (
  input  S,
  input  in_2,
  output out_3,
  output out_4
);

  nand nand_1 (out_3, S, out_4);
  nand nand_2 (out_4, out_3, in_2);

  // Notes on the sheet:
  //   _
  //   R
endmodule

module newSynRs (
  input  S,
  input  CP,
  input  R,
  output out_4,
  output out_5
);

  wire nand_1_out, nand_2_out;

  nand nand_1 (nand_1_out, S, CP);
  nand nand_2 (nand_2_out, CP, R);
  nand nand_3 (out_4, nand_1_out, out_5);
  nand nand_4 (out_5, out_4, nand_2_out);

  // Notes on the sheet:
  //   _
  //   S
  //   _
  //   R
endmodule

module newD (
  input  S,
  input  CP,
  output out_3,
  output out_4
);

  wire nand_1_out, nand_2_out, not_1_out;

  not not_1 (not_1_out, S);
  nand nand_1 (nand_1_out, S, CP);
  nand nand_2 (nand_2_out, CP, not_1_out);
  nand nand_3 (out_3, nand_1_out, out_4);
  nand nand_4 (out_4, out_3, nand_2_out);

  // Notes on the sheet:
  //   _
  //   S
  //   _
  //   R
endmodule

module jk (
  input  in_1,
  input  in_2,
  input  in_3,
  output out_4,
  output out_5
);

  wire and_1_out, d_2_out_3, nor_1_out, nor_2_out, not_1_out;

  nor nor_1 (nor_1_out, out_5, in_1);
  and and_1 (and_1_out, out_5, in_3);
  nor nor_2 (nor_2_out, nor_1_out, and_1_out);
  D d_1 (.out_3(out_5), .out_4(out_4), .in_1(d_2_out_3), .in_2(not_1_out));
  not not_1 (not_1_out, in_2);
  D d_2 (.out_3(d_2_out_3), .in_1(nor_2_out), .in_2(in_2));  // open: out_4
endmodule
