// Logisim project add31.circ as structural Verilog: 9 circuits, main circuit main
// A3
module main (
  input  A2,
  input  A1,
  input  A0,
  input  B2,
  input  B1,
  input  B0,
  output C,
  output S2,
  output S1,
  output S0
);

  wire fa_1_co, fa_2_co;

  fa fa_1 (.Ci(A1), .B(B1), .A(fa_2_co), .S(S1), .Co(fa_1_co));
  fa fa_2 (.Ci(1'b0), .B(A0), .A(B0), .S(S0), .Co(fa_2_co));
  fa fa_3 (.Ci(A2), .B(B2), .A(fa_1_co), .S(S2), .Co(C));

  // Notes on the sheet:
  //   Ci
endmodule

// HA
module ha (
  input  B,
  input  A,
  output S,
  output C
);

  wire and_1_out, and_2_out, not_1_out, not_2_out;

  not not_1 (not_1_out, B);
  not not_2 (not_2_out, A);
  and and_1 (and_1_out, A, not_1_out);
  and and_2 (and_2_out, B, not_2_out);
  and and_3 (C, B, A);
  or or_1 (S, and_1_out, and_2_out);
endmodule

// FA
module fa (
  input  Ci,
  input  B,
  input  A,
  output S,
  output Co
);

  wire ha_1_c, ha_2_c, ha_2_s;

  ha ha_1 (.B(Ci), .A(ha_2_s), .S(S), .C(ha_1_c));
  ha ha_2 (.B(B), .A(A), .S(ha_2_s), .C(ha_2_c));
  or or_1 (Co, ha_1_c, ha_2_c);

  // Notes on the sheet:
  //   C
  //   S
endmodule

module add3 (
  input  A2,
  input  A1,
  input  A0,
  input  B2,
  input  B1,
  input  B0,
  output C,
  output S2,
  output S1,
  output S0
);

  wire fa_1_co, fa_2_co;

  fa fa_1 (.Ci(A1), .B(B1), .A(fa_2_co), .S(S1), .Co(fa_1_co));
  fa fa_2 (.Ci(1'b0), .B(A0), .A(B0), .S(S0), .Co(fa_2_co));
  fa fa_3 (.Ci(A2), .B(B2), .A(fa_1_co), .S(S2), .Co(C));

  // Notes on the sheet:
  //   Ci
endmodule

// ALU
module arith (
  input  A2,
  input  A1,
  input  A0,
  input  B2,
  input  B1,
  input  B0,
  input  in_7,
  output C,
  output S2,
  output S1,
  output S0
);

  wire fa_1_co, fa_2_co, fa_3_co, not_1_out, not_2_out, not_3_out, not_4_out, not_5_out, selector_1_out_12,
       selector_1_out_13, selector_1_out_14, selector_1_out_15;

  not not_1 (not_1_out, A2);
  not not_2 (not_2_out, A1);
  not not_3 (not_3_out, A0);
  not not_4 (not_4_out, 1'b0);
  not not_5 (not_5_out, fa_3_co);
  selector selector_1 (
    .in_1(A2), .in_2(not_1_out), .in_3(A1), .in_4(not_2_out), .in_5(A0), .in_6(not_3_out), .in_7(1'b0),
    .in_8(not_4_out), .in_9(fa_3_co), .in_10(not_5_out), .in_11(in_7), .out_12(selector_1_out_12),
    .out_13(selector_1_out_13), .out_14(selector_1_out_14), .out_15(selector_1_out_15), .out_16(C));
  fa fa_1 (.Ci(B1), .B(selector_1_out_13), .A(fa_2_co), .S(S1), .Co(fa_1_co));
  fa fa_2 (.Ci(selector_1_out_15), .B(B0), .A(selector_1_out_14), .S(S0), .Co(fa_2_co));
  fa fa_3 (.Ci(B2), .B(selector_1_out_12), .A(fa_1_co), .S(S2), .Co(fa_3_co));

  // Notes on the sheet:
  //   A2
  //   A1
  //   A0
  //   C
  //   A2
  //   A1
  //   A0
  //   Ci
endmodule

module selector (
  input  in_1,
  input  in_2,
  input  in_3,
  input  in_4,
  input  in_5,
  input  in_6,
  input  in_7,
  input  in_8,
  input  in_9,
  input  in_10,
  input  in_11,
  output out_12,
  output out_13,
  output out_14,
  output out_15,
  output out_16
);

  wire not_1_out;

  assign out_12 = not_1_out ? in_1 : 1'bz;  // Controlled_Buffer controlled_buffer_1
  assign out_12 = in_11 ? in_2 : 1'bz;  // Controlled_Buffer controlled_buffer_2
  assign out_13 = not_1_out ? in_3 : 1'bz;  // Controlled_Buffer controlled_buffer_3
  assign out_13 = in_11 ? in_4 : 1'bz;  // Controlled_Buffer controlled_buffer_4
  assign out_14 = not_1_out ? in_5 : 1'bz;  // Controlled_Buffer controlled_buffer_5
  assign out_14 = in_11 ? in_6 : 1'bz;  // Controlled_Buffer controlled_buffer_6
  assign out_15 = not_1_out ? in_7 : 1'bz;  // Controlled_Buffer controlled_buffer_7
  assign out_15 = in_11 ? in_8 : 1'bz;  // Controlled_Buffer controlled_buffer_8
  assign out_16 = not_1_out ? in_9 : 1'bz;  // Controlled_Buffer controlled_buffer_9
  assign out_16 = in_11 ? in_10 : 1'bz;  // Controlled_Buffer controlled_buffer_10
  not not_1 (not_1_out, in_11);
endmodule

module zeroIf (
  input  in_1,
  input  in_2,
  input  in_3,
  input  in_4,
  output out_5
);

  wire not_1_out, not_2_out, not_3_out, not_4_out;

  not not_1 (not_1_out, in_1);
  not not_2 (not_2_out, in_2);
  not not_3 (not_3_out, in_3);
  not not_4 (not_4_out, in_4);
  and and_1 (out_5, not_1_out, not_2_out, not_3_out, not_4_out);
endmodule

// ALU
module arithZIF (
  input  B2,
  input  B1,
  input  B0,
  input  A2,
  input  A1,
  input  A0,
  input  in_7,
  output S2,
  output S1,
  output S0,
  output C,
  output out_12
);

  wire fa_1_co, fa_2_co, fa_3_co, not_1_out, not_2_out, not_3_out, not_4_out, not_5_out, selector_1_out_12,
       selector_1_out_13, selector_1_out_14, selector_1_out_15;

  not not_1 (not_1_out, A2);
  not not_2 (not_2_out, A1);
  not not_3 (not_3_out, A0);
  not not_4 (not_4_out, 1'b0);
  not not_5 (not_5_out, fa_3_co);
  selector selector_1 (
    .in_1(A2), .in_2(not_1_out), .in_3(A1), .in_4(not_2_out), .in_5(A0), .in_6(not_3_out), .in_7(1'b0),
    .in_8(not_4_out), .in_9(fa_3_co), .in_10(not_5_out), .in_11(in_7), .out_12(selector_1_out_12),
    .out_13(selector_1_out_13), .out_14(selector_1_out_14), .out_15(selector_1_out_15), .out_16(C));
  fa fa_1 (.Ci(B1), .B(selector_1_out_13), .A(fa_2_co), .S(S1), .Co(fa_1_co));
  fa fa_2 (.Ci(selector_1_out_15), .B(B0), .A(selector_1_out_14), .S(S0), .Co(fa_2_co));
  fa fa_3 (.Ci(B2), .B(selector_1_out_12), .A(fa_1_co), .S(S2), .Co(fa_3_co));
  zeroIf zeroif_1 (.in_1(C), .in_2(S2), .in_3(S1), .in_4(S0), .out_5(out_12));

  // Notes on the sheet:
  //   Ci
  //   Z
endmodule

module AIF (
  input  A2,
  input  A1,
  input  A0,
  input  B2,
  input  B1,
  input  B0,
  input  in_7,
  output C,
  output S2,
  output S1,
  output S0,
  output out_12
);

  wire fa_1_co, fa_2_co, fa_3_co, not_1_out, not_2_out, not_3_out, not_4_out, not_5_out, selector_1_out_12,
       selector_1_out_13, selector_1_out_14, selector_1_out_15;

  not not_1 (not_1_out, A2);
  not not_2 (not_2_out, A1);
  not not_3 (not_3_out, A0);
  not not_4 (not_4_out, 1'b0);
  not not_5 (not_5_out, fa_3_co);
  selector selector_1 (
    .in_1(A2), .in_2(not_1_out), .in_3(A1), .in_4(not_2_out), .in_5(A0), .in_6(not_3_out), .in_7(1'b0),
    .in_8(not_4_out), .in_9(fa_3_co), .in_10(not_5_out), .in_11(in_7), .out_12(selector_1_out_12),
    .out_13(selector_1_out_13), .out_14(selector_1_out_14), .out_15(selector_1_out_15), .out_16(C));
  fa fa_1 (.Ci(B1), .B(selector_1_out_13), .A(fa_2_co), .S(S1), .Co(fa_1_co));
  fa fa_2 (.Ci(selector_1_out_15), .B(B0), .A(selector_1_out_14), .S(S0), .Co(fa_2_co));
  fa fa_3 (.Ci(B2), .B(selector_1_out_12), .A(fa_1_co), .S(S2), .Co(fa_3_co));
  zeroIf zeroif_1 (.in_1(S0), .in_2(S1), .in_3(S2), .in_4(C), .out_5(out_12));

  // Notes on the sheet:
  //   -+
  //   A2
  //   A1
  //   A0
  //   C
  //   A2
  //   A1
  //   A0
  //   Ci
  //   Z
endmodule
