// Logisim project controller.circ as structural Verilog: 2 circuits, main circuit main
// Ctr3
module main (
  input  in_1,
  input  in_2,
  input  in_3,
  input  in_4,
  output out_5,
  output out_6,
  output out_7
);

  assign out_5 = in_1 ? in_2 : 1'bz;  // Controlled_Buffer controlled_buffer_1
  assign out_6 = in_1 ? in_3 : 1'bz;  // Controlled_Buffer controlled_buffer_2
  assign out_7 = in_1 ? in_4 : 1'bz;  // Controlled_Buffer controlled_buffer_3
endmodule

// C4
module c4 (
  input  in_1,
  input  in_2,
  input  in_3,
  input  in_4,
  input  in_5,
  output out_6,
  output out_7,
  output out_8,
  output out_9
);

  assign out_6 = in_1 ? in_2 : 1'bz;  // Controlled_Buffer controlled_buffer_1
  assign out_7 = in_1 ? in_3 : 1'bz;  // Controlled_Buffer controlled_buffer_2
  assign out_8 = in_1 ? in_4 : 1'bz;  // Controlled_Buffer controlled_buffer_3
  assign out_9 = in_1 ? in_5 : 1'bz;  // Controlled_Buffer controlled_buffer_4
endmodule
