// Logisim project 一个简单的8位计算机0.circ as structural Verilog
module _8_3 (
  input  i0,
  input  i1,
  input  i2,
  input  i3,
  input  i4,
  input  i5,
  input  i6,
  input  i7,
  output y0,
  output y1,
  output y2
);

  or or_1 (y0, i1, i3, i5, i7);
  or or_2 (y1, i2, i3, i6, i7);
  or or_3 (y2, i4, i5, i6, i7);
endmodule

module _138 (
  input  in_1,
  input  in_2,
  input  in_3,
  output out_4,
  output out_5,
  output out_6,
  output out_7,
  output out_8,
  output out_9,
  output out_10,
  output out_11
);

  wire not_1_out, not_2_out, not_3_out;

  not not_1 (not_1_out, in_1);
  not not_2 (not_2_out, in_2);
  not not_3 (not_3_out, in_3);
  and and_1 (out_4, not_1_out, not_2_out, not_3_out);
  and and_2 (out_5, in_1, not_2_out, not_3_out);
  and and_3 (out_6, not_1_out, in_2, not_3_out);
  and and_4 (out_7, in_1, in_2, not_3_out);
  and and_5 (out_8, not_1_out, not_2_out, in_3);
  and and_6 (out_9, in_1, not_2_out, in_3);
  and and_7 (out_10, not_1_out, in_2, in_3);
  and and_8 (out_11, in_1, in_2, in_3);
endmodule

// CN
module counter3 (
  input  T_CE,
  output out_2,
  output out_3,
  output out_4
);

  wire clock_1_out, not_1_out, not_2_out;

  Clock clock_1 (.out(clock_1_out));
  not not_1 (not_1_out, out_2);
  not not_2 (not_2_out, out_3);
  T_Flip_Flop t_ff_1 (.clk(clock_1_out), .T(T_CE), .Q(out_2));  // open: Qn, preset, reset, en
  T_Flip_Flop t_ff_2 (.clk(not_1_out), .T(T_CE), .Q(out_3));  // open: Qn, preset, reset, en
  T_Flip_Flop t_ff_3 (.clk(not_2_out), .T(T_CE), .Q(out_4));  // open: Qn, preset, reset, en

  // Notes on the sheet:
  //   CP
endmodule

module CS2 (
  input  \自动_手动 ,
  input  SEG,
  input  SEG_2,
  input  KEY,
  input  KEY_2,
  input  KEY_3,
  input  KEY_4,
  input  R0,
  input  R0_2,
  input  Rd,
  input  Rd_2,
  input  R1,
  input  R1_2,
  input  in_14,
  input  AO,
  input  OCP,
  input  in_17,
  input  OCP_2,
  input  in_19,
  input  AO_2,
  input  in_21,
  output out_22,
  output out_23,
  output out_24,
  output out_25,
  output out_26,
  output out_27,
  output out_28,
  output out_29,
  output out_30
);

  wire not_1_out;

  assign out_22 = not_1_out ? SEG : 1'bz;  // Controlled_Buffer controlled_buffer_1
  assign out_23 = not_1_out ? KEY : 1'bz;  // Controlled_Buffer controlled_buffer_2
  assign out_24 = not_1_out ? KEY_3 : 1'bz;  // Controlled_Buffer controlled_buffer_3
  assign out_25 = not_1_out ? R0 : 1'bz;  // Controlled_Buffer controlled_buffer_4
  assign out_26 = not_1_out ? Rd : 1'bz;  // Controlled_Buffer controlled_buffer_5
  assign out_27 = not_1_out ? R1 : 1'bz;  // Controlled_Buffer controlled_buffer_6
  assign out_28 = not_1_out ? in_14 : 1'bz;  // Controlled_Buffer controlled_buffer_7
  assign out_29 = not_1_out ? OCP_2 : 1'bz;  // Controlled_Buffer controlled_buffer_8
  assign out_30 = not_1_out ? AO_2 : 1'bz;  // Controlled_Buffer controlled_buffer_9
  not not_1 (not_1_out, \自动_手动 );
  assign out_22 = \自动_手动  ? SEG_2 : 1'bz;  // Controlled_Buffer controlled_buffer_10
  assign out_23 = \自动_手动  ? KEY_2 : 1'bz;  // Controlled_Buffer controlled_buffer_11
  assign out_24 = \自动_手动  ? KEY_4 : 1'bz;  // Controlled_Buffer controlled_buffer_12
  assign out_25 = \自动_手动  ? R0_2 : 1'bz;  // Controlled_Buffer controlled_buffer_13
  assign out_26 = \自动_手动  ? Rd_2 : 1'bz;  // Controlled_Buffer controlled_buffer_14
  assign out_27 = \自动_手动  ? R1_2 : 1'bz;  // Controlled_Buffer controlled_buffer_15
  assign out_28 = \自动_手动  ? in_17 : 1'bz;  // Controlled_Buffer controlled_buffer_16
  assign out_30 = \自动_手动  ? AO : 1'bz;  // Controlled_Buffer controlled_buffer_17
  assign out_29 = \自动_手动  ? OCP : 1'bz;  // Controlled_Buffer controlled_buffer_18

  // Notes on the sheet:
  //   手动
  //   手动
  //   -+
  //   自动
endmodule

// C24
module C224 (
  input  in_1,
  input  in_2,
  input  in_3,
  input  in_4,
  input  in_5,
  output out_6,
  output out_7,
  output out_8,
  output out_9,
  output out_10,
  output out_11,
  output out_12,
  output out_13
);

  wire not_1_out;

  assign out_7 = in_5 ? in_1 : 1'bz;  // Controlled_Buffer controlled_buffer_1
  assign out_8 = in_5 ? in_2 : 1'bz;  // Controlled_Buffer controlled_buffer_2
  assign out_9 = in_5 ? in_3 : 1'bz;  // Controlled_Buffer controlled_buffer_3
  assign out_6 = in_5 ? in_4 : 1'bz;  // Controlled_Buffer controlled_buffer_4
  not not_1 (not_1_out, in_5);
  assign out_10 = not_1_out ? in_1 : 1'bz;  // Controlled_Buffer controlled_buffer_5
  assign out_11 = not_1_out ? in_2 : 1'bz;  // Controlled_Buffer controlled_buffer_6
  assign out_12 = not_1_out ? in_3 : 1'bz;  // Controlled_Buffer controlled_buffer_7
  assign out_13 = not_1_out ? in_4 : 1'bz;  // Controlled_Buffer controlled_buffer_8
endmodule

module main3 (
  input  \输入0 ,
  input  _1,
  input  _2,
  input  _3,
  input  _4,
  input  _6,
  input  _7,
  input  \输入1 ,
  input  _1_2,
  input  \地址总线 ,
  input  _3_2,
  input  _4_2,
  input  _5,
  input  _6_2,
  input  in_15,
  input  _7_2,
  input  SEG,
  input  KEY,
  input  KEY_2,
  input  R0,
  input  Rd,
  input  R1,
  input  in_23,
  input  OCP,
  input  AO
);

  wire aif_1_c, aif_1_out_12, aif_1_s0, aif_1_s1, aif_1_s2, c4_1_out_6, c4_1_out_7, c4_1_out_8, c4_1_out_9,
       c4_3_out_6, c4_3_out_7, c4_3_out_8, c4_3_out_9, c224_1_out_10, c224_1_out_11, c224_1_out_12,
       cs2_1_out_22, cs2_1_out_23, cs2_1_out_24, cs2_1_out_25, cs2_1_out_26, cs2_1_out_27, cs2_1_out_28,
       cs2_1_out_29, cs2_1_out_30, digital_1_a, digital_1_b, digital_1_c, digital_1_d, digital_1_e,
       digital_1_f, digital_1_g, n8_3_1_y0, n8_3_1_y1, n8_3_1_y2, n8_3_2_y0, n8_3_2_y1, n8_3_2_y2,
       n138_1_out_4, n138_1_out_5, n138_1_out_6, n138_1_out_7, n138_1_out_8, n138_1_out_9, n138_1_out_10,
       n138_1_out_11, r33_1_out_5, r33_1_out_6, r33_1_out_7, r33_2_out_5, r33_2_out_6, r33_2_out_7, undriven;
  wire [2:0] counter3_1_out_2;
  wire [8:0] rom_1_data;

  _8_3 u_8_3_1 (
    .i0(\输入0 ), .i1(_1), .i2(_2), .i3(_3), .i4(_4), .i5(undriven), .i6(_6), .i7(_7), .y0(n8_3_1_y0),
    .y1(n8_3_1_y1), .y2(n8_3_1_y2));
  _8_3 u_8_3_2 (
    .i0(\输入1 ), .i1(_1_2), .i2(1'b1), .i3(_3_2), .i4(_4_2), .i5(_5), .i6(_6_2), .i7(_7_2), .y0(n8_3_2_y0),
    .y1(n8_3_2_y1), .y2(n8_3_2_y2));
  LED led_1 (.in(c4_1_out_8));
  LED led_2 (.in(c4_1_out_9));
  c4 c4_1 (
    .in_2(n8_3_1_y0), .in_3(n8_3_1_y1), .in_4(n8_3_1_y2), .in_5(1'b0), .in_1(cs2_1_out_23),
    .out_6(c4_1_out_6), .out_7(c4_1_out_7), .out_8(c4_1_out_8), .out_9(c4_1_out_9));
  c4 c4_2 (
    .in_2(n8_3_2_y0), .in_3(n8_3_2_y1), .in_4(n8_3_2_y2), .in_5(1'b0), .in_1(cs2_1_out_24),
    .out_6(c4_1_out_6), .out_7(c4_1_out_7), .out_8(c4_1_out_8), .out_9(c4_1_out_9));
  CS2 cs2_1 (
    .SEG(SEG), .KEY(KEY), .KEY_3(KEY_2), .R0(R0), .Rd(Rd), .R1(R1), .in_14(in_23), .out_22(cs2_1_out_22),
    .out_23(cs2_1_out_23), .out_24(cs2_1_out_24), .out_25(cs2_1_out_25), .out_26(cs2_1_out_26),
    .out_27(cs2_1_out_27), .out_28(cs2_1_out_28), .out_29(cs2_1_out_29), .out_30(cs2_1_out_30), .OCP_2(OCP),
    .AO_2(AO), .AO(rom_1_data[0]), .OCP(rom_1_data[1]), .in_17(rom_1_data[2]), .\自动_手动 (\地址总线 ),
    .SEG_2(rom_1_data[8]), .KEY_2(rom_1_data[7]), .KEY_4(rom_1_data[6]), .R0_2(rom_1_data[5]),
    .Rd_2(rom_1_data[4]), .R1_2(rom_1_data[3]));  // open: in_19, in_21
  LED led_3 (.in(c4_1_out_7));
  LED led_4 (.in(c4_1_out_6));
  R33 r33_1 (
    .out_5(r33_1_out_5), .out_6(r33_1_out_6), .out_7(r33_1_out_7), .in_2(c4_1_out_8), .in_3(c4_1_out_7),
    .in_4(c4_1_out_6), .in_1(cs2_1_out_25));
  R33 r33_2 (
    .out_5(r33_2_out_5), .out_6(r33_2_out_6), .out_7(r33_2_out_7), .in_2(c4_1_out_8), .in_3(c4_1_out_7),
    .in_4(c4_1_out_6), .in_1(cs2_1_out_27));
  LED led_5 (.in(rom_1_data[7]));
  LED led_6 (.in(rom_1_data[8]));
  Digital digital_1 (
    .D0(c4_3_out_6), .D1(c4_3_out_7), .D2(c4_3_out_8), .D3(c4_3_out_9), .a(digital_1_a), .b(digital_1_b),
    .c(digital_1_c), .d(digital_1_d), .e(digital_1_e), .f(digital_1_f), .g(digital_1_g));
  c4 c4_3 (
    .in_2(c4_1_out_9), .in_3(c4_1_out_8), .in_4(c4_1_out_7), .in_5(c4_1_out_6), .in_1(cs2_1_out_22),
    .out_6(c4_3_out_6), .out_7(c4_3_out_7), .out_8(c4_3_out_8), .out_9(c4_3_out_9));
  C224 c224_1 (
    .in_1(r33_1_out_5), .in_2(r33_1_out_6), .in_3(r33_1_out_7), .in_4(1'b0), .out_6(c4_1_out_9),
    .out_7(c4_1_out_8), .out_8(c4_1_out_7), .out_9(c4_1_out_6), .in_5(cs2_1_out_26), .out_10(c224_1_out_10),
    .out_11(c224_1_out_11), .out_12(c224_1_out_12));  // open: out_13
  LED led_7 (.in(rom_1_data[6]));
  LED led_8 (.in(rom_1_data[4]));
  LED led_9 (.in(rom_1_data[3]));
  LED led_10 (.in(rom_1_data[5]));
  _7_Segment_Display #(.active("false")) u_7_segment_display_1 (
    .g(digital_1_g), .f(digital_1_f), .a(digital_1_a), .b(digital_1_b), .e(digital_1_e), .d(digital_1_d),
    .c(digital_1_c), .dp(1'b1));
  AIF aif_1 (
    .A2(c224_1_out_10), .A1(c224_1_out_11), .A0(c224_1_out_12), .B2(r33_2_out_5), .B1(r33_2_out_6),
    .B0(r33_2_out_7), .out_12(aif_1_out_12), .in_7(cs2_1_out_28), .C(aif_1_c), .S2(aif_1_s2), .S1(aif_1_s1),
    .S0(aif_1_s0));
  LED led_11 (.in(aif_1_out_12));
  LED led_12 (.in(rom_1_data[2]));
  LED led_13 (.in(rom_1_data[1]));
  LED led_14 (.in(rom_1_data[0]));
  MS3C ms3c_1 (
    .in_1(cs2_1_out_30), .out_7(c4_1_out_9), .out_8(c4_1_out_8), .out_9(c4_1_out_7), .out_10(c4_1_out_6),
    .in_3(aif_1_c), .in_4(aif_1_s2), .in_5(aif_1_s1), .in_6(aif_1_s0), .in_2(cs2_1_out_29));
  counter3 counter3_1 (
    .T_CE(\地址总线 ), .out_2(counter3_1_out_2[0]), .out_3(counter3_1_out_2[1]), .out_4(counter3_1_out_2[2]));
  _138 u_138_1 (
    .in_1(counter3_1_out_2[0]), .in_2(counter3_1_out_2[1]), .in_3(counter3_1_out_2[2]), .out_4(n138_1_out_4),
    .out_5(n138_1_out_5), .out_6(n138_1_out_6), .out_7(n138_1_out_7), .out_8(n138_1_out_8),
    .out_9(n138_1_out_9), .out_10(n138_1_out_10), .out_11(n138_1_out_11));
  ROM #(.addrWidth(3), .dataWidth(9)) rom_1 (.addr(counter3_1_out_2), .data(rom_1_data), .sel(in_15));
  LED led_15 (.in(n138_1_out_4));
  LED led_16 (.in(n138_1_out_5));
  LED led_17 (.in(n138_1_out_6));
  LED led_18 (.in(n138_1_out_7));
  LED led_19 (.in(n138_1_out_8));
  LED led_20 (.in(n138_1_out_9));
  LED led_21 (.in(n138_1_out_10));
  LED led_22 (.in(n138_1_out_11));

  // Notes on the sheet:
  //   “外码"
  //   0
  //   0
  //   2
  //   手自切换
  //   “内码”
  //   数据总线
  //   累加器A
  //   寄存器B
  //   “外码"
  //   AO
  //   运算器
  //   -+
  //   OCP
  //   输出
  //   控制总线
  //   门电路造计算机
  //   加法程序5+2=7
  //   2018.4.7.19:57
  //   Shou
  //   带置位计数器
  //   自动/手动
  //   contents of rom_1 (hex, n*v repeats v):
  //   1a0 180 118 110 160 142 121 110
  //   Input I1
  //   Mov A,B
  //   Input I2
  //   Add B
  //   Output
endmodule
