// Logisim project 乘法器.circ as structural Verilog: 8 circuits, main circuit main
module main (
  input  in_1,
  input  \高位 ,
  input  in_3,
  input  in_4,
  input  in_5,
  input  \低位 ,
  input  in_7,
  input  in_8,
  input  in_9,
  input  _7,
  input  in_11,
  input  in_12,
  input  in_13,
  input  in_14,
  input  in_15,
  input  in_16,
  input  _0,
  input  _0_2,
  input  in_19,
  input  in_20,
  input  in_21,
  input  in_22,
  input  in_23,
  input  in_24,
  input  _7_2,
  input  in_26,
  output out_27,
  output out_28,
  output out_29,
  output out_30,
  output out_31,
  output out_32,
  output out_33,
  output out_34,
  output out_35,
  output out_36,
  output out_37,
  output out_38,
  output out_39,
  output out_40,
  output out_41,
  output out_42,
  output out_43,
  output out_44,
  output out_45,
  output out_46,
  output out_47,
  output out_48,
  output out_49,
  output out_50
);

  wire n2seg_1_out_10, n2seg_1_out_11, n2seg_1_out_12, n2seg_1_out_13, n2seg_1_out_14, n2seg_1_out_15,
       n2seg_1_out_16, n2seg_1_out_17, n2seg_1_out_18, n2seg_1_out_19, n2seg_1_out_20, n2seg_1_out_21,
       n2seg_1_out_22, n2seg_1_out_23;

  LED #(.active("true")) led_1 (.in(\低位 ));
  LED #(.active("true")) led_2 (.in(in_8));
  LED #(.active("true")) led_3 (.in(in_5));
  LED #(.active("true")) led_4 (.in(in_7));
  LED #(.active("true")) led_5 (.in(in_1));
  LED #(.active("true")) led_6 (.in(in_3));
  LED #(.active("true")) led_7 (.in(in_4));
  LED #(.active("true")) led_8 (.in(\高位 ));
  \四乘四位乘法器  \u_四乘四位乘法器_1  (
    .in_5(in_5), .in_6(\低位 ), .in_7(in_7), .in_8(in_8), .out_10(out_34), .out_11(out_33), .out_12(out_32),
    .out_13(out_31), .out_14(out_30), .out_15(out_29), .out_16(out_28), .out_17(out_27), .in_2(in_1),
    .in_3(\高位 ), .in_1(in_3), .in_4(in_4), .in_9(in_9));
  _8_8 u_8_8_1 (
    .in_9(_0_2), .in_10(in_19), .in_11(in_20), .in_12(in_21), .in_13(in_22), .in_14(in_23), .in_15(in_24),
    .in_16(_7_2), .out_18(out_35), .out_19(out_36), .out_20(out_37), .out_21(out_38), .out_22(out_39),
    .out_23(out_40), .out_24(out_41), .out_25(out_42), .out_26(out_43), .out_27(out_44), .out_28(out_45),
    .out_29(out_46), .out_30(out_47), .out_31(out_48), .out_32(out_49), .out_33(out_50), .in_1(_0),
    .in_2(in_16), .in_3(in_15), .in_4(in_14), .in_6(in_13), .in_7(in_12), .in_8(in_11), .in_5(_7),
    .in_17(in_26));
  _2seg u_2seg_1 (
    .i0(out_34), .i1(out_33), .i2(out_32), .i3(out_31), .i4(out_30), .i5(out_29), .i6(out_28), .i7(out_27),
    .out_10(n2seg_1_out_10), .out_11(n2seg_1_out_11), .out_12(n2seg_1_out_12), .out_13(n2seg_1_out_13),
    .out_14(n2seg_1_out_14), .out_15(n2seg_1_out_15), .out_16(n2seg_1_out_16), .out_17(n2seg_1_out_17),
    .out_18(n2seg_1_out_18), .out_19(n2seg_1_out_19), .out_20(n2seg_1_out_20), .out_21(n2seg_1_out_21),
    .out_22(n2seg_1_out_22), .out_23(n2seg_1_out_23), .in_2(in_9));
  _7_Segment_Display #(.active("false")) u_7_segment_display_1 (
    .g(n2seg_1_out_23), .f(n2seg_1_out_22), .a(n2seg_1_out_17), .b(n2seg_1_out_18), .e(n2seg_1_out_21),
    .d(n2seg_1_out_20), .c(n2seg_1_out_19), .dp(1'b1));
  _7_Segment_Display #(.active("false")) u_7_segment_display_2 (
    .g(n2seg_1_out_16), .f(n2seg_1_out_15), .a(n2seg_1_out_10), .b(n2seg_1_out_11), .e(n2seg_1_out_14),
    .d(n2seg_1_out_13), .c(n2seg_1_out_12), .dp(1'b1));

  // Notes on the sheet:
  //   低位二极管显示
  //   高位
  //   高位二进制
  //   低位
  //   结果
  //   十六进制输出
endmodule

module \半加器  (
  input  \加数 ,
  input  \加数_2 ,
  output \个位 ,
  output \十位 
);

  xor xor_1 (\个位 , \加数 , \加数_2 );
  and and_1 (\十位 , \加数 , \加数_2 );
endmodule

module \全加器  (
  input  \前一次运算的进位 ,
  input  \加数 ,
  input  \加数_2 ,
  output \和 ,
  output \运算产生的进位 
);

  wire \半加器_1_个位 , \半加器_1_十位 , \半加器_2_十位 ;

  \半加器  \u_半加器_1  (.\加数 (\加数 ), .\加数_2 (\加数_2 ), .\个位 (\半加器_1_个位 ), .\十位 (\半加器_1_十位 ));
  \半加器  \u_半加器_2  (.\加数 (\前一次运算的进位 ), .\加数_2 (\半加器_1_个位 ), .\个位 (\和 ), .\十位 (\半加器_2_十位 ));
  or or_1 (\运算产生的进位 , \半加器_2_十位 , \半加器_1_十位 );
endmodule

module \一位乘法器  (
  input  \乘数 ,
  input  \上一运算的进位 ,
  input  \乘数_2 ,
  input  \上一运算的和 ,
  output \积 ,
  output \进位 
);

  wire and_1_out;

  and and_1 (and_1_out, \乘数 , \乘数_2 );
  \全加器  \u_全加器_1  (.\前一次运算的进位 (\上一运算的进位 ), .\加数 (and_1_out), .\加数_2 (\上一运算的和 ), .\和 (\积 ), .\运算产生的进位 (\进位 ));
endmodule

// 一位乘法器
module \四位乘法器  (
  input  \乘数 ,
  input  \上一运算的进位 ,
  input  \乘数_2 ,
  input  \上一运算的积 ,
  input  in_5,
  input  in_6,
  input  in_7,
  input  in_8,
  input  in_9,
  input  in_10,
  output \积 ,
  output out_12,
  output out_13,
  output out_14,
  output out_15
);

  wire and_1_out, and_2_out, and_3_out, and_4_out, \全加器_1_运算产生的进位 , \全加器_2_运算产生的进位 , \全加器_3_运算产生的进位 ;

  and and_1 (and_1_out, \乘数 , \乘数_2 );
  and and_2 (and_2_out, \乘数 , in_5);
  and and_3 (and_3_out, \乘数 , in_7);
  and and_4 (and_4_out, \乘数 , in_9);
  \全加器  \u_全加器_1  (.\前一次运算的进位 (\上一运算的进位 ), .\加数 (and_1_out), .\加数_2 (\上一运算的积 ), .\和 (\积 ), .\运算产生的进位 (\全加器_1_运算产生的进位 ));
  \全加器  \u_全加器_2  (
    .\前一次运算的进位 (\全加器_1_运算产生的进位 ), .\加数 (and_2_out), .\加数_2 (in_6), .\和 (out_12), .\运算产生的进位 (\全加器_2_运算产生的进位 ));
  \全加器  \u_全加器_3  (
    .\前一次运算的进位 (\全加器_2_运算产生的进位 ), .\加数 (and_3_out), .\加数_2 (in_8), .\和 (out_13), .\运算产生的进位 (\全加器_3_运算产生的进位 ));
  \全加器  \u_全加器_4  (.\前一次运算的进位 (\全加器_3_运算产生的进位 ), .\加数 (and_4_out), .\加数_2 (in_10), .\和 (out_14), .\运算产生的进位 (out_15));

  // Notes on the sheet:
  //   进位
endmodule

// 4*4乘法器
module \四乘四位乘法器  (
  input  in_1,
  input  in_2,
  input  in_3,
  input  in_4,
  input  in_5,
  input  in_6,
  input  in_7,
  input  in_8,
  input  in_9,
  output out_10,
  output out_11,
  output out_12,
  output out_13,
  output out_14,
  output out_15,
  output out_16,
  output out_17
);

  wire and_1_out, and_2_out, and_3_out, and_4_out, \四位乘法器_1_out_12 , \四位乘法器_1_out_13 , \四位乘法器_1_out_14 ,
       \四位乘法器_1_out_15 , \四位乘法器_2_out_12 , \四位乘法器_2_out_13 , \四位乘法器_2_out_14 , \四位乘法器_2_out_15 ,
       \四位乘法器_3_out_12 , \四位乘法器_3_out_13 , \四位乘法器_3_out_14 , \四位乘法器_3_out_15 ;

  and and_1 (and_1_out, in_5, in_9);
  and and_2 (and_2_out, in_6, in_9);
  and and_3 (and_3_out, in_7, in_9);
  and and_4 (and_4_out, in_8, in_9);
  \四位乘法器  \u_四位乘法器_1  (
    .\乘数_2 (and_1_out), .\上一运算的积 (1'b0), .in_5(and_2_out), .in_6(1'b0), .in_7(and_3_out), .in_8(1'b0),
    .in_9(and_4_out), .in_10(1'b0), .\积 (out_10), .out_12(\四位乘法器_1_out_12 ), .out_13(\四位乘法器_1_out_13 ),
    .out_14(\四位乘法器_1_out_14 ), .out_15(\四位乘法器_1_out_15 ), .\乘数 (in_2), .\上一运算的进位 (1'b0));
  \四位乘法器  \u_四位乘法器_2  (
    .\乘数_2 (and_1_out), .\上一运算的积 (\四位乘法器_1_out_12 ), .in_5(and_2_out), .in_6(\四位乘法器_1_out_13 ),
    .in_7(and_3_out), .in_8(\四位乘法器_1_out_14 ), .in_9(and_4_out), .in_10(\四位乘法器_1_out_15 ), .\积 (out_11),
    .out_12(\四位乘法器_2_out_12 ), .out_13(\四位乘法器_2_out_13 ), .out_14(\四位乘法器_2_out_14 ),
    .out_15(\四位乘法器_2_out_15 ), .\乘数 (in_3), .\上一运算的进位 (1'b0));
  \四位乘法器  \u_四位乘法器_3  (
    .\乘数_2 (and_1_out), .\上一运算的积 (\四位乘法器_2_out_12 ), .in_5(and_2_out), .in_6(\四位乘法器_2_out_13 ),
    .in_7(and_3_out), .in_8(\四位乘法器_2_out_14 ), .in_9(and_4_out), .in_10(\四位乘法器_2_out_15 ), .\积 (out_12),
    .out_12(\四位乘法器_3_out_12 ), .out_13(\四位乘法器_3_out_13 ), .out_14(\四位乘法器_3_out_14 ),
    .out_15(\四位乘法器_3_out_15 ), .\乘数 (in_1), .\上一运算的进位 (1'b0));
  \四位乘法器  \u_四位乘法器_4  (
    .\乘数_2 (and_1_out), .\上一运算的积 (\四位乘法器_3_out_12 ), .in_5(and_2_out), .in_6(\四位乘法器_3_out_13 ),
    .in_7(and_3_out), .in_8(\四位乘法器_3_out_14 ), .in_9(and_4_out), .in_10(\四位乘法器_3_out_15 ), .\积 (out_13),
    .out_12(out_14), .out_13(out_15), .out_14(out_16), .out_15(out_17), .\乘数 (in_4), .\上一运算的进位 (1'b0));
endmodule

module _1_8 (
  input  \乘数 ,
  input  \上一运算的进位 ,
  input  \乘数_2 ,
  input  \上一运算的积 ,
  input  in_5,
  input  in_6,
  input  in_7,
  input  in_8,
  input  in_9,
  input  in_10,
  input  \乘数_3 ,
  input  \上一运算的积_2 ,
  input  in_13,
  input  in_14,
  input  in_15,
  input  in_16,
  input  in_17,
  input  in_18,
  output \积 ,
  output out_20,
  output out_21,
  output out_22,
  output \积_2 ,
  output out_24,
  output out_25,
  output out_26,
  output out_27
);

  wire and_1_out, and_2_out, and_3_out, and_4_out, and_5_out, and_6_out, and_7_out, and_8_out,
       \全加器_1_运算产生的进位 , \全加器_2_运算产生的进位 , \全加器_3_运算产生的进位 , \全加器_4_运算产生的进位 , \全加器_5_运算产生的进位 , \全加器_6_运算产生的进位 ,
       \全加器_7_运算产生的进位 ;

  and and_1 (and_1_out, \乘数 , \乘数_2 );
  and and_2 (and_2_out, \乘数 , in_5);
  and and_3 (and_3_out, \乘数 , in_7);
  and and_4 (and_4_out, \乘数 , in_9);
  and and_5 (and_5_out, \乘数 , \乘数_3 );
  and and_6 (and_6_out, \乘数 , in_13);
  and and_7 (and_7_out, \乘数 , in_15);
  and and_8 (and_8_out, \乘数 , in_17);
  \全加器  \u_全加器_1  (.\前一次运算的进位 (\上一运算的进位 ), .\加数 (and_1_out), .\加数_2 (\上一运算的积 ), .\和 (\积 ), .\运算产生的进位 (\全加器_1_运算产生的进位 ));
  \全加器  \u_全加器_2  (
    .\前一次运算的进位 (\全加器_1_运算产生的进位 ), .\加数 (and_2_out), .\加数_2 (in_6), .\和 (out_20), .\运算产生的进位 (\全加器_2_运算产生的进位 ));
  \全加器  \u_全加器_3  (
    .\前一次运算的进位 (\全加器_2_运算产生的进位 ), .\加数 (and_3_out), .\加数_2 (in_8), .\和 (out_21), .\运算产生的进位 (\全加器_3_运算产生的进位 ));
  \全加器  \u_全加器_4  (
    .\前一次运算的进位 (\全加器_3_运算产生的进位 ), .\加数 (and_4_out), .\加数_2 (in_10), .\和 (out_22), .\运算产生的进位 (\全加器_4_运算产生的进位 ));
  \全加器  \u_全加器_5  (
    .\前一次运算的进位 (\全加器_4_运算产生的进位 ), .\加数 (and_5_out), .\加数_2 (\上一运算的积_2 ), .\和 (\积_2 ),
    .\运算产生的进位 (\全加器_5_运算产生的进位 ));
  \全加器  \u_全加器_6  (
    .\前一次运算的进位 (\全加器_5_运算产生的进位 ), .\加数 (and_6_out), .\加数_2 (in_14), .\和 (out_24), .\运算产生的进位 (\全加器_6_运算产生的进位 ));
  \全加器  \u_全加器_7  (
    .\前一次运算的进位 (\全加器_6_运算产生的进位 ), .\加数 (and_7_out), .\加数_2 (in_16), .\和 (out_25), .\运算产生的进位 (\全加器_7_运算产生的进位 ));
  \全加器  \u_全加器_8  (.\前一次运算的进位 (\全加器_7_运算产生的进位 ), .\加数 (and_8_out), .\加数_2 (in_18), .\和 (out_26), .\运算产生的进位 (out_27));

  // Notes on the sheet:
  //   进位
  //   进位
endmodule

module _8_8 (
  input  in_1,
  input  in_2,
  input  in_3,
  input  in_4,
  input  in_5,
  input  in_6,
  input  in_7,
  input  in_8,
  input  in_9,
  input  in_10,
  input  in_11,
  input  in_12,
  input  in_13,
  input  in_14,
  input  in_15,
  input  in_16,
  input  in_17,
  output out_18,
  output out_19,
  output out_20,
  output out_21,
  output out_22,
  output out_23,
  output out_24,
  output out_25,
  output out_26,
  output out_27,
  output out_28,
  output out_29,
  output out_30,
  output out_31,
  output out_32,
  output out_33
);

  wire and_1_out, and_2_out, and_3_out, and_4_out, and_5_out, and_6_out, and_7_out, and_8_out, n1_8_1_out_20,
       n1_8_1_out_21, n1_8_1_out_22, n1_8_1_out_24, n1_8_1_out_25, n1_8_1_out_26, n1_8_1_out_27,
       \n1_8_1_积_2 , n1_8_2_out_20, n1_8_2_out_21, n1_8_2_out_22, n1_8_2_out_24, n1_8_2_out_25,
       n1_8_2_out_26, n1_8_2_out_27, \n1_8_2_积_2 , n1_8_3_out_20, n1_8_3_out_21, n1_8_3_out_22,
       n1_8_3_out_24, n1_8_3_out_25, n1_8_3_out_26, n1_8_3_out_27, \n1_8_3_积_2 , n1_8_4_out_20,
       n1_8_4_out_21, n1_8_4_out_22, n1_8_4_out_24, n1_8_4_out_25, n1_8_4_out_26, n1_8_4_out_27,
       \n1_8_4_积_2 , n1_8_5_out_20, n1_8_5_out_21, n1_8_5_out_22, n1_8_5_out_24, n1_8_5_out_25,
       n1_8_5_out_26, n1_8_5_out_27, \n1_8_5_积_2 , n1_8_6_out_20, n1_8_6_out_21, n1_8_6_out_22,
       n1_8_6_out_24, n1_8_6_out_25, n1_8_6_out_26, n1_8_6_out_27, \n1_8_6_积_2 , n1_8_7_out_20,
       n1_8_7_out_21, n1_8_7_out_22, n1_8_7_out_24, n1_8_7_out_25, n1_8_7_out_26, n1_8_7_out_27, \n1_8_7_积_2 ;

  and and_1 (and_1_out, in_9, in_17);
  and and_2 (and_2_out, in_10, in_17);
  and and_3 (and_3_out, in_11, in_17);
  and and_4 (and_4_out, in_12, in_17);
  and and_5 (and_5_out, in_13, in_17);
  and and_6 (and_6_out, in_14, in_17);
  and and_7 (and_7_out, in_15, in_17);
  and and_8 (and_8_out, in_16, in_17);
  _1_8 u_1_8_1 (
    .\乘数_2 (and_1_out), .\上一运算的积 (1'b0), .in_5(and_2_out), .in_6(1'b0), .in_7(and_3_out), .in_8(1'b0),
    .in_9(and_4_out), .in_10(1'b0), .\乘数_3 (and_5_out), .\上一运算的积_2 (1'b0), .in_13(and_6_out), .in_14(1'b0),
    .in_15(and_7_out), .in_16(1'b0), .in_17(and_8_out), .in_18(1'b0), .\乘数 (in_1), .\上一运算的进位 (1'b0),
    .\积 (out_18), .out_20(n1_8_1_out_20), .out_21(n1_8_1_out_21), .out_22(n1_8_1_out_22),
    .\积_2 (\n1_8_1_积_2 ), .out_24(n1_8_1_out_24), .out_25(n1_8_1_out_25), .out_26(n1_8_1_out_26),
    .out_27(n1_8_1_out_27));
  _1_8 u_1_8_2 (
    .\乘数_2 (and_1_out), .\上一运算的积 (n1_8_1_out_20), .in_5(and_2_out), .in_6(n1_8_1_out_21), .in_7(and_3_out),
    .in_8(n1_8_1_out_22), .in_9(and_4_out), .in_10(\n1_8_1_积_2 ), .\乘数_3 (and_5_out),
    .\上一运算的积_2 (n1_8_1_out_24), .in_13(and_6_out), .in_14(n1_8_1_out_25), .in_15(and_7_out),
    .in_16(n1_8_1_out_26), .in_17(and_8_out), .in_18(n1_8_1_out_27), .\乘数 (in_2), .\上一运算的进位 (1'b0),
    .\积 (out_19), .out_20(n1_8_2_out_20), .out_21(n1_8_2_out_21), .out_22(n1_8_2_out_22),
    .\积_2 (\n1_8_2_积_2 ), .out_24(n1_8_2_out_24), .out_25(n1_8_2_out_25), .out_26(n1_8_2_out_26),
    .out_27(n1_8_2_out_27));
  _1_8 u_1_8_3 (
    .\乘数_2 (and_1_out), .\上一运算的积 (n1_8_2_out_20), .in_5(and_2_out), .in_6(n1_8_2_out_21), .in_7(and_3_out),
    .in_8(n1_8_2_out_22), .in_9(and_4_out), .in_10(\n1_8_2_积_2 ), .\乘数_3 (and_5_out),
    .\上一运算的积_2 (n1_8_2_out_24), .in_13(and_6_out), .in_14(n1_8_2_out_25), .in_15(and_7_out),
    .in_16(n1_8_2_out_26), .in_17(and_8_out), .in_18(n1_8_2_out_27), .\乘数 (in_3), .\上一运算的进位 (1'b0),
    .\积 (out_20), .out_20(n1_8_3_out_20), .out_21(n1_8_3_out_21), .out_22(n1_8_3_out_22),
    .\积_2 (\n1_8_3_积_2 ), .out_24(n1_8_3_out_24), .out_25(n1_8_3_out_25), .out_26(n1_8_3_out_26),
    .out_27(n1_8_3_out_27));
  _1_8 u_1_8_4 (
    .\乘数_2 (and_1_out), .\上一运算的积 (n1_8_3_out_20), .in_5(and_2_out), .in_6(n1_8_3_out_21), .in_7(and_3_out),
    .in_8(n1_8_3_out_22), .in_9(and_4_out), .in_10(\n1_8_3_积_2 ), .\乘数_3 (and_5_out),
    .\上一运算的积_2 (n1_8_3_out_24), .in_13(and_6_out), .in_14(n1_8_3_out_25), .in_15(and_7_out),
    .in_16(n1_8_3_out_26), .in_17(and_8_out), .in_18(n1_8_3_out_27), .\乘数 (in_4), .\上一运算的进位 (1'b0),
    .\积 (out_21), .out_20(n1_8_4_out_20), .out_21(n1_8_4_out_21), .out_22(n1_8_4_out_22),
    .\积_2 (\n1_8_4_积_2 ), .out_24(n1_8_4_out_24), .out_25(n1_8_4_out_25), .out_26(n1_8_4_out_26),
    .out_27(n1_8_4_out_27));
  _1_8 u_1_8_5 (
    .\乘数_2 (and_1_out), .\上一运算的积 (n1_8_4_out_20), .in_5(and_2_out), .in_6(n1_8_4_out_21), .in_7(and_3_out),
    .in_8(n1_8_4_out_22), .in_9(and_4_out), .in_10(\n1_8_4_积_2 ), .\乘数_3 (and_5_out),
    .\上一运算的积_2 (n1_8_4_out_24), .in_13(and_6_out), .in_14(n1_8_4_out_25), .in_15(and_7_out),
    .in_16(n1_8_4_out_26), .in_17(and_8_out), .in_18(n1_8_4_out_27), .\乘数 (in_6), .\上一运算的进位 (1'b0),
    .\积 (out_22), .out_20(n1_8_5_out_20), .out_21(n1_8_5_out_21), .out_22(n1_8_5_out_22),
    .\积_2 (\n1_8_5_积_2 ), .out_24(n1_8_5_out_24), .out_25(n1_8_5_out_25), .out_26(n1_8_5_out_26),
    .out_27(n1_8_5_out_27));
  _1_8 u_1_8_6 (
    .\乘数_2 (and_1_out), .\上一运算的积 (n1_8_5_out_20), .in_5(and_2_out), .in_6(n1_8_5_out_21), .in_7(and_3_out),
    .in_8(n1_8_5_out_22), .in_9(and_4_out), .in_10(\n1_8_5_积_2 ), .\乘数_3 (and_5_out),
    .\上一运算的积_2 (n1_8_5_out_24), .in_13(and_6_out), .in_14(n1_8_5_out_25), .in_15(and_7_out),
    .in_16(n1_8_5_out_26), .in_17(and_8_out), .in_18(n1_8_5_out_27), .\乘数 (in_7), .\上一运算的进位 (1'b0),
    .\积 (out_23), .out_20(n1_8_6_out_20), .out_21(n1_8_6_out_21), .out_22(n1_8_6_out_22),
    .\积_2 (\n1_8_6_积_2 ), .out_24(n1_8_6_out_24), .out_25(n1_8_6_out_25), .out_26(n1_8_6_out_26),
    .out_27(n1_8_6_out_27));
  _1_8 u_1_8_7 (
    .\乘数_2 (and_1_out), .\上一运算的积 (n1_8_6_out_20), .in_5(and_2_out), .in_6(n1_8_6_out_21), .in_7(and_3_out),
    .in_8(n1_8_6_out_22), .in_9(and_4_out), .in_10(\n1_8_6_积_2 ), .\乘数_3 (and_5_out),
    .\上一运算的积_2 (n1_8_6_out_24), .in_13(and_6_out), .in_14(n1_8_6_out_25), .in_15(and_7_out),
    .in_16(n1_8_6_out_26), .in_17(and_8_out), .in_18(n1_8_6_out_27), .\乘数 (in_8), .\上一运算的进位 (1'b0),
    .\积 (out_24), .out_20(n1_8_7_out_20), .out_21(n1_8_7_out_21), .out_22(n1_8_7_out_22),
    .\积_2 (\n1_8_7_积_2 ), .out_24(n1_8_7_out_24), .out_25(n1_8_7_out_25), .out_26(n1_8_7_out_26),
    .out_27(n1_8_7_out_27));
  _1_8 u_1_8_8 (
    .\乘数_2 (and_1_out), .\上一运算的积 (n1_8_7_out_20), .in_5(and_2_out), .in_6(n1_8_7_out_21), .in_7(and_3_out),
    .in_8(n1_8_7_out_22), .in_9(and_4_out), .in_10(\n1_8_7_积_2 ), .\乘数_3 (and_5_out),
    .\上一运算的积_2 (n1_8_7_out_24), .in_13(and_6_out), .in_14(n1_8_7_out_25), .in_15(and_7_out),
    .in_16(n1_8_7_out_26), .in_17(and_8_out), .in_18(n1_8_7_out_27), .\乘数 (in_5), .\上一运算的进位 (1'b0),
    .\积 (out_25), .out_20(out_26), .out_21(out_27), .out_22(out_28), .\积_2 (out_29), .out_24(out_30),
    .out_25(out_31), .out_26(out_32), .out_27(out_33));
endmodule
