// Logisim project 集成电路（终极版）.circ as structural Verilog: 6 circuits, main circuit LED计数器电路
module \LED计数器电路  (
  input  in_1,
  input  in_2,
  input  in_3,
  input  in_4,
  input  in_5,
  output out_6,
  output out_7,
  output out_8,
  output out_9,
  output out_10
);

  or or_1 (out_6, in_1, in_2, in_3, in_4, in_5);
  or or_2 (out_7, in_2, in_3, in_4, in_5);
  or or_3 (out_8, in_3, in_4, in_5);
  or or_4 (out_9, in_4, in_5);

  assign out_10 = in_5;
endmodule

module \LED计数器封装  (
);

  wire _1_out, _2_out, _3_out, _4_out, _5_out, \led计数器电路_1_out_6 , \led计数器电路_1_out_7 , \led计数器电路_1_out_8 ,
       \led计数器电路_1_out_9 , \led计数器电路_1_out_10 ;

  Button _1 (.out(_1_out));
  Button _2 (.out(_2_out));
  Button _3 (.out(_3_out));
  Button _4 (.out(_4_out));
  Button _5 (.out(_5_out));
  \LED计数器电路  \led计数器电路_1  (
    .in_1(_1_out), .in_2(_2_out), .in_3(_3_out), .in_4(_4_out), .in_5(_5_out), .out_6(\led计数器电路_1_out_6 ),
    .out_7(\led计数器电路_1_out_7 ), .out_8(\led计数器电路_1_out_8 ), .out_9(\led计数器电路_1_out_9 ),
    .out_10(\led计数器电路_1_out_10 ));
  LED #(.active("true")) led_1 (.in(\led计数器电路_1_out_6 ));
  LED #(.active("true")) led_2 (.in(\led计数器电路_1_out_7 ));
  LED #(.active("true")) led_3 (.in(\led计数器电路_1_out_8 ));
  LED #(.active("true")) led_4 (.in(\led计数器电路_1_out_9 ));
  LED #(.active("true")) led_5 (.in(\led计数器电路_1_out_10 ));
endmodule

module \_5输入按键编码器  (
  input  In1,
  input  In2,
  input  In3,
  input  In4,
  input  In5,
  output Out1,
  output Out2,
  output Out3
);

  wire and_1_out, and_2_out, and_3_out, and_4_out, and_5_out, not_1_out, not_2_out, not_3_out, not_4_out,
       not_5_out, not_6_out, not_7_out, not_8_out, not_9_out;

  not not_1 (not_1_out, In4);
  not not_2 (not_2_out, In2);
  not not_3 (not_3_out, In4);
  not not_4 (not_4_out, In4);
  not not_5 (not_5_out, In5);
  not not_6 (not_6_out, In3);
  not not_7 (not_7_out, In4);
  not not_8 (not_8_out, In5);
  not not_9 (not_9_out, In5);
  and and_1 (and_1_out, In3, not_1_out);
  and and_2 (and_2_out, In1, not_2_out, not_3_out);
  and and_3 (and_3_out, In3, not_4_out, not_5_out);
  and and_4 (and_4_out, In2, not_6_out, not_7_out, not_8_out);
  and and_5 (and_5_out, In4, not_9_out);
  or or_1 (Out1, In5, and_1_out, and_2_out);
  or or_2 (Out2, and_3_out, and_4_out);
  or or_3 (Out3, In5, and_5_out);
endmodule

module \_5输入按键显示器  (
);

  wire _1_out, _2_out, _3_out, _4_out, _5_out, \led计数器电路_1_out_6 , \led计数器电路_1_out_7 , \led计数器电路_1_out_8 ,
       \led计数器电路_1_out_9 , \led计数器电路_1_out_10 ;
  wire [2:0] \n5输入按键编码器_1_out1 ;

  Button _1 (.out(_1_out));
  Button _2 (.out(_2_out));
  Button _3 (.out(_3_out));
  Button _4 (.out(_4_out));
  Button _5 (.out(_5_out));
  \LED计数器电路  \led计数器电路_1  (
    .in_1(_1_out), .in_2(_2_out), .in_3(_3_out), .in_4(_4_out), .in_5(_5_out), .out_6(\led计数器电路_1_out_6 ),
    .out_7(\led计数器电路_1_out_7 ), .out_8(\led计数器电路_1_out_8 ), .out_9(\led计数器电路_1_out_9 ),
    .out_10(\led计数器电路_1_out_10 ));
  \_5输入按键编码器  \u_5输入按键编码器_1  (
    .In1(_1_out), .In2(_2_out), .In3(_3_out), .In4(_4_out), .In5(_5_out), .Out1(\n5输入按键编码器_1_out1 [0]),
    .Out2(\n5输入按键编码器_1_out1 [1]), .Out3(\n5输入按键编码器_1_out1 [2]));
  LED #(.active("true")) led_1 (.in(\led计数器电路_1_out_6 ));
  LED #(.active("true")) led_2 (.in(\led计数器电路_1_out_7 ));
  LED #(.active("true")) led_3 (.in(\led计数器电路_1_out_8 ));
  LED #(.active("true")) led_4 (.in(\led计数器电路_1_out_9 ));
  LED #(.active("true")) led_5 (.in(\led计数器电路_1_out_10 ));
  // Probe on \n5输入按键编码器_1_out1 
  Hex_Digit_Display hex_digit_display_1 (.value({1'b0, \n5输入按键编码器_1_out1 }), .dp(1'b1));
endmodule

module \_7段数码管显示驱动  (
  input  A,
  input  B,
  input  C,
  input  D,
  output out_5,
  output out_6,
  output out_7,
  output out_8,
  output out_9,
  output out_10,
  output out_11
);

  a a_1 (.A(A), .B(B), .C(C), .D(D), .a_2(out_5));
  b b_1 (.A(A), .B(B), .C(C), .D(D), .b_2(out_6));
  c c_1 (.A(A), .B(B), .C(C), .D(D), .c_2(out_7));
  d d_1 (.A(A), .B(B), .C(C), .D(D), .d_2(out_8));
  e e_1 (.A(A), .B(B), .C(C), .D(D), .e(out_9));
  f f_1 (.A(A), .B(B), .C(C), .D(D), .f(out_10));
  g g_1 (.A(A), .B(B), .C(C), .D(D), .g(out_11));
endmodule

module \集成电路  (
);

  wire _1_out, _2_out, _3_out, _4_out, _5_out, \led计数器电路_1_out_6 , \led计数器电路_1_out_7 , \led计数器电路_1_out_8 ,
       \led计数器电路_1_out_9 , \led计数器电路_1_out_10 , seg_1_out_5, seg_1_out_6, seg_1_out_7, seg_1_out_8,
       seg_1_out_9, seg_1_out_10, seg_1_out_11;
  wire [2:0] \n5输入按键编码器_1_out1 ;

  Button _1 (.out(_1_out));
  Button _2 (.out(_2_out));
  Button _3 (.out(_3_out));
  Button _4 (.out(_4_out));
  Button _5 (.out(_5_out));
  \LED计数器电路  \led计数器电路_1  (
    .in_1(_1_out), .in_2(_2_out), .in_3(_3_out), .in_4(_4_out), .in_5(_5_out), .out_6(\led计数器电路_1_out_6 ),
    .out_7(\led计数器电路_1_out_7 ), .out_8(\led计数器电路_1_out_8 ), .out_9(\led计数器电路_1_out_9 ),
    .out_10(\led计数器电路_1_out_10 ));
  \_5输入按键编码器  \u_5输入按键编码器_1  (
    .In1(_1_out), .In2(_2_out), .In3(_3_out), .In4(_4_out), .In5(_5_out), .Out1(\n5输入按键编码器_1_out1 [0]),
    .Out2(\n5输入按键编码器_1_out1 [1]), .Out3(\n5输入按键编码器_1_out1 [2]));
  LED #(.active("true")) led_1 (.in(\led计数器电路_1_out_6 ));
  LED #(.active("true")) led_2 (.in(\led计数器电路_1_out_7 ));
  LED #(.active("true")) led_3 (.in(\led计数器电路_1_out_8 ));
  LED #(.active("true")) led_4 (.in(\led计数器电路_1_out_9 ));
  LED #(.active("true")) led_5 (.in(\led计数器电路_1_out_10 ));
  // Probe on \n5输入按键编码器_1_out1 
  Hex_Digit_Display hex_digit_display_1 (.value({1'b0, \n5输入按键编码器_1_out1 }), .dp(1'b1));
  seg seg_1 (
    .A(1'b0), .B(\n5输入按键编码器_1_out1 [2]), .C(\n5输入按键编码器_1_out1 [1]), .D(\n5输入按键编码器_1_out1 [0]),
    .out_5(seg_1_out_5), .out_6(seg_1_out_6), .out_7(seg_1_out_7), .out_8(seg_1_out_8), .out_9(seg_1_out_9),
    .out_10(seg_1_out_10), .out_11(seg_1_out_11));
  _7_Segment_Display #(.active("true")) u_7_segment_display_1 (
    .g(seg_1_out_11), .f(seg_1_out_10), .a(seg_1_out_5), .b(seg_1_out_6), .e(seg_1_out_9), .d(seg_1_out_8),
    .c(seg_1_out_7), .dp(1'b1));
endmodule
